// Logisim project blip.circ as structural Verilog: 1 circuit, main circuit main
module main (
  input  RESET
);

  wire CLK_out, multiplexer_1_out, TAKEN;
  wire [4:0] UBR_NEAR_sw1;
  wire [11:0] bit_extender_1_out, BRANCH_COND, UPC, UPC_BR, UPC_INC, UPC_NEXT, WIDE_TARGET;

  Clock CLK (.out(CLK_out));
  DipSwitch #(.number(5)) UBR_NEAR (
    .sw1(UBR_NEAR_sw1[0]), .sw2(UBR_NEAR_sw1[1]), .sw3(UBR_NEAR_sw1[2]), .sw4(UBR_NEAR_sw1[3]),
    .sw5(UBR_NEAR_sw1[4]));
  Register #(.width(12)) u_uPC (.D(UPC_NEXT), .en(1'b1), .clk(CLK_out), .Q(UPC), .clr(RESET));
  Multiplexer #(.select(4)) multiplexer_1 (
    .in0(1'b0), .out(multiplexer_1_out), .sel(4'b0000));  // open: in1, in2, in3, in4, in5, in6, in7, in8, in9, in10, in11, in12, in13, in14, in15
  assign bit_extender_1_out = {{7{UBR_NEAR_sw1[4]}}, UBR_NEAR_sw1};  // Bit_Extender bit_extender_1
  xor xor_1 (TAKEN, multiplexer_1_out, 1'b1);
  Adder #(.width(12)) adder_1 (.a(bit_extender_1_out), .b(UPC), .out(UPC_BR));  // open: cin, cout
  // Probe on UPC
  // Probe on UPC_INC
  Adder #(.width(12)) adder_2 (.a(UPC), .b(12'h1), .out(UPC_INC));  // open: cin, cout
  // Probe on UPC_NEXT
  Multiplexer #(.select(3), .width(12)) multiplexer_2 (
    .in0(UPC_INC), .in1(WIDE_TARGET), .in4(BRANCH_COND), .out(UPC_NEXT), .sel(3'b100));  // open: in2, in3, in5, in6, in7
  // Probe on UPC_BR
  Multiplexer #(.width(12)) multiplexer_3 (.in0(UPC_INC), .in1(UPC_BR), .out(BRANCH_COND), .sel(TAKEN));
endmodule
