// Logisim project control_word_decoder.circ as structural Verilog: 1 circuit, main circuit control_word_decoder
module control_word_decoder (
  input  cw_dp_0,
  input  cw_dp_1,
  input  cw_dp_2,
  input  cw_dp_3,
  input  cw_dp_4,
  input  cw_dp_5,
  input  cw_dp_6,
  input  cw_dp_7,
  input  cw_dp_8,
  input  cw_dp_9,
  input  cw_dp_10,
  input  cw_dp_11,
  input  cw_dp_12,
  input  cw_dp_13,
  input  cw_dp_14,
  input  cw_dp_15,
  input  cw_dp_16,
  input  cw_dp_17,
  input  cw_dp_18,
  input  cw_dp_19,
  input  cw_dp_20,
  input  cw_dp_21,
  input  cw_dp_22,
  input  cw_dp_23,
  input  cw_dp_24,
  input  cw_dp_25,
  input  cw_dp_26,
  input  cw_dp_27,
  input  cw_dp_28,
  input  cw_dp_29,
  input  cw_dp_30,
  input  cw_dp_31,
  input  cw_dp_32,
  input  cw_dp_33,
  input  cw_dp_34,
  input  cw_dp_35,
  input  cw_dp_36,
  input  cw_dp_37,
  input  cw_dp_38,
  input  cw_dp_39,
  input  cw_dp_40,
  input  cw_dp_41,
  input  cw_dp_42,
  input  cw_dp_43,
  input  cw_dp_44,
  input  cw_dp_45,
  input  cw_dp_46,
  input  cw_dp_47,
  input  cw_dp_48,
  input  cw_dp_49,
  input  cw_dp_50,
  input  cw_dp_51,
  input  cw_dp_52,
  input  cw_dp_53,
  input  cw_dp_54,
  input  cw_dp_55,
  input  cw_dp_56,
  input  cw_dp_57,
  input  cw_dp_58,
  input  cw_dp_59,
  input  cw_dp_60,
  input  cw_dp_61,
  input  cw_dp_62,
  input  cw_dp_63,
  output ir_load_n_0,
  output ir_load_n_1,
  output ir_load_n_2,
  output ir_load_n_3,
  output left_src_n_0,
  output left_src_n_1,
  output left_src_n_2,
  output left_src_n_3,
  output left_src_n_4,
  output left_src_n_5,
  output left_src_n_6,
  output left_src_n_7,
  output left_src_n_8,
  output left_src_n_9,
  output left_src_n_10,
  output left_src_n_11,
  output left_src_n_12,
  output left_src_n_13,
  output left_src_n_14,
  output left_src_n_15,
  output left_lane_n_0,
  output left_lane_n_1,
  output left_lane_n_2,
  output left_lane_n_3,
  output right_src_n_0,
  output right_src_n_1,
  output right_src_n_2,
  output right_src_n_3,
  output right_src_n_4,
  output right_src_n_5,
  output right_src_n_6,
  output right_src_n_7,
  output alu_op_n_0,
  output alu_op_n_1,
  output alu_op_n_2,
  output alu_op_n_3,
  output alu_op_n_4,
  output alu_op_n_5,
  output alu_op_n_6,
  output alu_op_n_7,
  output alu_op_n_8,
  output alu_op_n_9,
  output alu_op_n_10,
  output alu_op_n_11,
  output alu_op_n_12,
  output alu_op_n_13,
  output alu_op_n_14,
  output alu_op_n_15,
  output alu_shift_n_0,
  output alu_shift_n_1,
  output alu_shift_n_2,
  output alu_shift_n_3,
  output alu_shift_n_4,
  output alu_shift_n_5,
  output alu_shift_n_6,
  output alu_shift_n_7,
  output v_src_n_0,
  output v_src_n_1,
  output v_src_n_2,
  output v_src_n_3,
  output c_src_n_0,
  output c_src_n_1,
  output c_src_n_2,
  output c_src_n_3,
  output cc_write_n_0,
  output cc_write_n_1,
  output cc_write_n_2,
  output cc_write_n_3,
  output cc_mi_n_0,
  output cc_mi_n_1,
  output cc_mi_n_2,
  output cc_mi_n_3,
  output z_dest_n_0,
  output z_dest_n_1,
  output z_dest_n_2,
  output z_dest_n_3,
  output z_dest_n_4,
  output z_dest_n_5,
  output z_dest_n_6,
  output z_dest_n_7,
  output z_dest_n_8,
  output z_dest_n_9,
  output z_dest_n_10,
  output z_dest_n_11,
  output z_dest_n_12,
  output z_dest_n_13,
  output z_dest_n_14,
  output z_dest_n_15,
  output z_lane_n_0,
  output z_lane_n_1,
  output z_lane_n_2,
  output z_lane_n_3,
  output pc_ctrl_n_0,
  output pc_ctrl_n_1,
  output pc_ctrl_n_2,
  output pc_ctrl_n_3,
  output mar_ctrl_n_0,
  output mar_ctrl_n_1,
  output mar_ctrl_n_2,
  output mar_ctrl_n_3,
  output x_ctrl_n_0,
  output x_ctrl_n_1,
  output x_ctrl_n_2,
  output x_ctrl_n_3,
  output y_ctrl_n_0,
  output y_ctrl_n_1,
  output y_ctrl_n_2,
  output y_ctrl_n_3,
  output mem_op_n_0,
  output mem_op_n_1,
  output mem_op_n_2,
  output mem_op_n_3,
  output mmu_addr_n_0,
  output mmu_addr_n_1,
  output mmu_addr_n_2,
  output mmu_addr_n_3,
  output mmu_map_n_0,
  output mmu_map_n_1,
  output mmu_map_n_2,
  output mmu_map_n_3,
  output mmu_pt_n_0,
  output mmu_pt_n_1,
  output mmu_pt_n_2,
  output mmu_pt_n_3,
  output alu_cin,
  output alu_width,
  output flag_we_0,
  output flag_we_1,
  output flag_we_2,
  output flag_we_3,
  output flag_we_4,
  output z_accum,
  output sp_bank,
  output tas_lock
);

  wire ONE, ZERO;

  _74138 a_sh (
    .pin1(cw_dp_15), .pin2(cw_dp_16), .pin3(cw_dp_17), .pin4(ZERO), .pin5(ZERO), .pin6(ONE),
    .pin7(alu_shift_n_7), .pin15(alu_shift_n_0), .pin14(alu_shift_n_1), .pin13(alu_shift_n_2),
    .pin12(alu_shift_n_3), .pin11(alu_shift_n_4), .pin10(alu_shift_n_5), .pin9(alu_shift_n_6));
  _74139 d3 (
    .pin1(ZERO), .pin2(cw_dp_38), .pin3(cw_dp_39), .pin4(z_lane_n_0), .pin5(z_lane_n_1), .pin6(z_lane_n_2),
    .pin7(z_lane_n_3), .pin15(ZERO), .pin14(cw_dp_40), .pin13(cw_dp_41), .pin12(pc_ctrl_n_0),
    .pin11(pc_ctrl_n_1), .pin10(pc_ctrl_n_2), .pin9(pc_ctrl_n_3));
  _74139 d7 (
    .pin1(ZERO), .pin2(cw_dp_54), .pin3(cw_dp_55), .pin4(mmu_pt_n_0), .pin5(mmu_pt_n_1), .pin6(mmu_pt_n_2),
    .pin7(mmu_pt_n_3), .pin15(ONE), .pin14(ZERO), .pin13(ZERO));  // open: pin12, pin11, pin10, pin9
  _74138 op_lo (
    .pin1(cw_dp_11), .pin2(cw_dp_12), .pin3(cw_dp_13), .pin4(cw_dp_14), .pin5(ZERO), .pin6(ONE),
    .pin7(alu_op_n_7), .pin15(alu_op_n_0), .pin14(alu_op_n_1), .pin13(alu_op_n_2), .pin12(alu_op_n_3),
    .pin11(alu_op_n_4), .pin10(alu_op_n_5), .pin9(alu_op_n_6));
  _74139 d4 (
    .pin1(ZERO), .pin2(cw_dp_42), .pin3(cw_dp_43), .pin4(mar_ctrl_n_0), .pin5(mar_ctrl_n_1),
    .pin6(mar_ctrl_n_2), .pin7(mar_ctrl_n_3), .pin15(ZERO), .pin14(cw_dp_44), .pin13(cw_dp_45),
    .pin12(x_ctrl_n_0), .pin11(x_ctrl_n_1), .pin10(x_ctrl_n_2), .pin9(x_ctrl_n_3));
  _74138 ls_hi (
    .pin1(cw_dp_2), .pin2(cw_dp_3), .pin3(cw_dp_4), .pin4(ZERO), .pin5(ZERO), .pin6(cw_dp_5),
    .pin7(left_src_n_15), .pin15(left_src_n_8), .pin14(left_src_n_9), .pin13(left_src_n_10),
    .pin12(left_src_n_11), .pin11(left_src_n_12), .pin10(left_src_n_13), .pin9(left_src_n_14));
  _74138 r_src (
    .pin1(cw_dp_8), .pin2(cw_dp_9), .pin3(cw_dp_10), .pin4(ZERO), .pin5(ZERO), .pin6(ONE),
    .pin7(right_src_n_7), .pin15(right_src_n_0), .pin14(right_src_n_1), .pin13(right_src_n_2),
    .pin12(right_src_n_3), .pin11(right_src_n_4), .pin10(right_src_n_5), .pin9(right_src_n_6));
  _74139 d1 (
    .pin1(ZERO), .pin2(cw_dp_25), .pin3(cw_dp_26), .pin4(v_src_n_0), .pin5(v_src_n_1), .pin6(v_src_n_2),
    .pin7(v_src_n_3), .pin15(ZERO), .pin14(cw_dp_27), .pin13(cw_dp_28), .pin12(c_src_n_0), .pin11(c_src_n_1),
    .pin10(c_src_n_2), .pin9(c_src_n_3));
  _74139 d5 (
    .pin1(ZERO), .pin2(cw_dp_46), .pin3(cw_dp_47), .pin4(y_ctrl_n_0), .pin5(y_ctrl_n_1), .pin6(y_ctrl_n_2),
    .pin7(y_ctrl_n_3), .pin15(ZERO), .pin14(cw_dp_48), .pin13(cw_dp_49), .pin12(mem_op_n_0),
    .pin11(mem_op_n_1), .pin10(mem_op_n_2), .pin9(mem_op_n_3));
  _74138 ls_lo (
    .pin1(cw_dp_2), .pin2(cw_dp_3), .pin3(cw_dp_4), .pin4(cw_dp_5), .pin5(ZERO), .pin6(ONE),
    .pin7(left_src_n_7), .pin15(left_src_n_0), .pin14(left_src_n_1), .pin13(left_src_n_2),
    .pin12(left_src_n_3), .pin11(left_src_n_4), .pin10(left_src_n_5), .pin9(left_src_n_6));
  _74138 zd_hi (
    .pin1(cw_dp_34), .pin2(cw_dp_35), .pin3(cw_dp_36), .pin4(ZERO), .pin5(ZERO), .pin6(cw_dp_37),
    .pin7(z_dest_n_15), .pin15(z_dest_n_8), .pin14(z_dest_n_9), .pin13(z_dest_n_10), .pin12(z_dest_n_11),
    .pin11(z_dest_n_12), .pin10(z_dest_n_13), .pin9(z_dest_n_14));
  _74139 d2 (
    .pin1(ZERO), .pin2(cw_dp_30), .pin3(cw_dp_31), .pin4(cc_write_n_0), .pin5(cc_write_n_1),
    .pin6(cc_write_n_2), .pin7(cc_write_n_3), .pin15(ZERO), .pin14(cw_dp_32), .pin13(cw_dp_33),
    .pin12(cc_mi_n_0), .pin11(cc_mi_n_1), .pin10(cc_mi_n_2), .pin9(cc_mi_n_3));
  _74139 d6 (
    .pin1(ZERO), .pin2(cw_dp_50), .pin3(cw_dp_51), .pin4(mmu_addr_n_0), .pin5(mmu_addr_n_1),
    .pin6(mmu_addr_n_2), .pin7(mmu_addr_n_3), .pin15(ZERO), .pin14(cw_dp_52), .pin13(cw_dp_53),
    .pin12(mmu_map_n_0), .pin11(mmu_map_n_1), .pin10(mmu_map_n_2), .pin9(mmu_map_n_3));
  _74138 op_hi (
    .pin1(cw_dp_11), .pin2(cw_dp_12), .pin3(cw_dp_13), .pin4(ZERO), .pin5(ZERO), .pin6(cw_dp_14),
    .pin7(alu_op_n_15), .pin15(alu_op_n_8), .pin14(alu_op_n_9), .pin13(alu_op_n_10), .pin12(alu_op_n_11),
    .pin11(alu_op_n_12), .pin10(alu_op_n_13), .pin9(alu_op_n_14));
  _74138 zd_lo (
    .pin1(cw_dp_34), .pin2(cw_dp_35), .pin3(cw_dp_36), .pin4(cw_dp_37), .pin5(ZERO), .pin6(ONE),
    .pin7(z_dest_n_7), .pin15(z_dest_n_0), .pin14(z_dest_n_1), .pin13(z_dest_n_2), .pin12(z_dest_n_3),
    .pin11(z_dest_n_4), .pin10(z_dest_n_5), .pin9(z_dest_n_6));
  _74139 d0 (
    .pin1(ZERO), .pin2(cw_dp_0), .pin3(cw_dp_1), .pin4(ir_load_n_0), .pin5(ir_load_n_1), .pin6(ir_load_n_2),
    .pin7(ir_load_n_3), .pin15(ZERO), .pin14(cw_dp_6), .pin13(cw_dp_7), .pin12(left_lane_n_0),
    .pin11(left_lane_n_1), .pin10(left_lane_n_2), .pin9(left_lane_n_3));

  assign alu_cin = cw_dp_18;
  assign alu_width = cw_dp_19;
  assign flag_we_0 = cw_dp_20;
  assign flag_we_1 = cw_dp_21;
  assign flag_we_2 = cw_dp_22;
  assign flag_we_3 = cw_dp_23;
  assign flag_we_4 = cw_dp_24;
  assign sp_bank = cw_dp_56;
  assign tas_lock = cw_dp_57;
  assign z_accum = cw_dp_29;
  // also tied to GND on the sheet: ZERO
  // also tied to VCC on the sheet: ONE

  // Other names for the same wires on the sheet: alu_op_0 = cw_dp_11; alu_op_1 = cw_dp_12; alu_op_2 = cw_dp_13;
  //   alu_op_3 = cw_dp_14; alu_shift_0 = cw_dp_15; alu_shift_1 = cw_dp_16; alu_shift_2 = cw_dp_17; c_src_0 = cw_dp_27;
  //   c_src_1 = cw_dp_28; cc_mi_0 = cw_dp_32; cc_mi_1 = cw_dp_33; cc_write_0 = cw_dp_30; cc_write_1 = cw_dp_31
endmodule
