// Logisim project cpu.circ as structural Verilog: 9 circuits, main circuit cpu
module _74574 (
  input  OE_n,
  input  D0,
  input  D1,
  input  D2,
  input  D3,
  input  D4,
  input  D5,
  input  D6,
  input  D7,
  input  CLK,
  output Q7,
  output Q6,
  output Q5,
  output Q4,
  output Q3,
  output Q2,
  output Q1,
  output Q0
);
endmodule

module sst39sf010a (
  input  a16,
  input  a15,
  input  a12,
  input  a7,
  input  a6,
  input  a5,
  input  a4,
  input  a3,
  input  a2,
  input  a1,
  input  a0,
  input  ce_n,
  input  a10,
  input  oe_n,
  input  a11,
  input  a9,
  input  a8,
  input  a13,
  input  a14,
  input  we_n,
  output dq0,
  output dq1,
  output dq2,
  output dq3,
  output dq4,
  output dq5,
  output dq6,
  output dq7
);
endmodule

module is61c64 (
  input  a12,
  input  a7,
  input  a6,
  input  a5,
  input  a4,
  input  a3,
  input  a2,
  input  a1,
  input  a0,
  input  ce_n,
  input  a10,
  input  oe_n,
  input  a11,
  input  a9,
  input  a8,
  input  we_n,
  output io0,
  output io1,
  output io2,
  output io3,
  output io4,
  output io5,
  output io6,
  output io7
);
endmodule

module control_word_decoder (
  input  [31:0] cw_dp__0,
  input  [31:0] cw_dp__1,
  output [3:0] ir_load_n,
  output [15:0] left_src_n,
  output [3:0] left_lane_n,
  output [7:0] right_src_n,
  output [15:0] alu_op_n,
  output [7:0] alu_shift_n,
  output [3:0] v_src_n,
  output [3:0] c_src_n,
  output [3:0] cc_write_n,
  output [3:0] cc_mi_n,
  output [15:0] z_dest_n,
  output [3:0] z_lane_n,
  output [3:0] pc_ctrl_n,
  output [3:0] mar_ctrl_n,
  output [3:0] x_ctrl_n,
  output [3:0] y_ctrl_n,
  output [3:0] mem_op_n,
  output [3:0] mmu_addr_n,
  output [3:0] mmu_map_n,
  output [3:0] mmu_pt_n,
  output alu_cin,
  output alu_width,
  output [4:0] flag_we,
  output z_accum,
  output sp_bank,
  output tas_lock
);

  wire ONE, ZERO;

  _74138 a_sh (
    .pin1(cw_dp__0[15]), .pin2(cw_dp__0[16]), .pin3(cw_dp__0[17]), .pin4(ZERO), .pin5(ZERO), .pin6(ONE),
    .pin7(alu_shift_n[7]), .pin15(alu_shift_n[0]), .pin14(alu_shift_n[1]), .pin13(alu_shift_n[2]),
    .pin12(alu_shift_n[3]), .pin11(alu_shift_n[4]), .pin10(alu_shift_n[5]), .pin9(alu_shift_n[6]));
  _74139 d3 (
    .pin1(ZERO), .pin2(cw_dp__1[6]), .pin3(cw_dp__1[7]), .pin4(z_lane_n[0]), .pin5(z_lane_n[1]),
    .pin6(z_lane_n[2]), .pin7(z_lane_n[3]), .pin15(ZERO), .pin14(cw_dp__1[8]), .pin13(cw_dp__1[9]),
    .pin12(pc_ctrl_n[0]), .pin11(pc_ctrl_n[1]), .pin10(pc_ctrl_n[2]), .pin9(pc_ctrl_n[3]));
  _74139 d7 (
    .pin1(ZERO), .pin2(cw_dp__1[22]), .pin3(cw_dp__1[23]), .pin4(mmu_pt_n[0]), .pin5(mmu_pt_n[1]),
    .pin6(mmu_pt_n[2]), .pin7(mmu_pt_n[3]), .pin15(ONE), .pin14(ZERO), .pin13(ZERO));  // open: pin12, pin11, pin10, pin9
  _74138 op_lo (
    .pin1(cw_dp__0[11]), .pin2(cw_dp__0[12]), .pin3(cw_dp__0[13]), .pin4(cw_dp__0[14]), .pin5(ZERO),
    .pin6(ONE), .pin7(alu_op_n[7]), .pin15(alu_op_n[0]), .pin14(alu_op_n[1]), .pin13(alu_op_n[2]),
    .pin12(alu_op_n[3]), .pin11(alu_op_n[4]), .pin10(alu_op_n[5]), .pin9(alu_op_n[6]));
  _74139 d0 (
    .pin1(ZERO), .pin2(cw_dp__0[0]), .pin3(cw_dp__0[1]), .pin4(ir_load_n[0]), .pin5(ir_load_n[1]),
    .pin6(ir_load_n[2]), .pin7(ir_load_n[3]), .pin15(ZERO), .pin14(cw_dp__0[6]), .pin13(cw_dp__0[7]),
    .pin12(left_lane_n[0]), .pin11(left_lane_n[1]), .pin10(left_lane_n[2]), .pin9(left_lane_n[3]));
  _74139 d4 (
    .pin1(ZERO), .pin2(cw_dp__1[10]), .pin3(cw_dp__1[11]), .pin4(mar_ctrl_n[0]), .pin5(mar_ctrl_n[1]),
    .pin6(mar_ctrl_n[2]), .pin7(mar_ctrl_n[3]), .pin15(ZERO), .pin14(cw_dp__1[12]), .pin13(cw_dp__1[13]),
    .pin12(x_ctrl_n[0]), .pin11(x_ctrl_n[1]), .pin10(x_ctrl_n[2]), .pin9(x_ctrl_n[3]));
  _74138 ls_hi (
    .pin1(cw_dp__0[2]), .pin2(cw_dp__0[3]), .pin3(cw_dp__0[4]), .pin4(ZERO), .pin5(ZERO), .pin6(cw_dp__0[5]),
    .pin7(left_src_n[15]), .pin15(left_src_n[8]), .pin14(left_src_n[9]), .pin13(left_src_n[10]),
    .pin12(left_src_n[11]), .pin11(left_src_n[12]), .pin10(left_src_n[13]), .pin9(left_src_n[14]));
  _74138 r_src (
    .pin1(cw_dp__0[8]), .pin2(cw_dp__0[9]), .pin3(cw_dp__0[10]), .pin4(ZERO), .pin5(ZERO), .pin6(ONE),
    .pin7(right_src_n[7]), .pin15(right_src_n[0]), .pin14(right_src_n[1]), .pin13(right_src_n[2]),
    .pin12(right_src_n[3]), .pin11(right_src_n[4]), .pin10(right_src_n[5]), .pin9(right_src_n[6]));
  _74139 d1 (
    .pin1(ZERO), .pin2(cw_dp__0[25]), .pin3(cw_dp__0[26]), .pin4(v_src_n[0]), .pin5(v_src_n[1]),
    .pin6(v_src_n[2]), .pin7(v_src_n[3]), .pin15(ZERO), .pin14(cw_dp__0[27]), .pin13(cw_dp__0[28]),
    .pin12(c_src_n[0]), .pin11(c_src_n[1]), .pin10(c_src_n[2]), .pin9(c_src_n[3]));
  _74139 d5 (
    .pin1(ZERO), .pin2(cw_dp__1[14]), .pin3(cw_dp__1[15]), .pin4(y_ctrl_n[0]), .pin5(y_ctrl_n[1]),
    .pin6(y_ctrl_n[2]), .pin7(y_ctrl_n[3]), .pin15(ZERO), .pin14(cw_dp__1[16]), .pin13(cw_dp__1[17]),
    .pin12(mem_op_n[0]), .pin11(mem_op_n[1]), .pin10(mem_op_n[2]), .pin9(mem_op_n[3]));
  _74138 ls_lo (
    .pin1(cw_dp__0[2]), .pin2(cw_dp__0[3]), .pin3(cw_dp__0[4]), .pin4(cw_dp__0[5]), .pin5(ZERO), .pin6(ONE),
    .pin7(left_src_n[7]), .pin15(left_src_n[0]), .pin14(left_src_n[1]), .pin13(left_src_n[2]),
    .pin12(left_src_n[3]), .pin11(left_src_n[4]), .pin10(left_src_n[5]), .pin9(left_src_n[6]));
  _74138 zd_hi (
    .pin1(cw_dp__1[2]), .pin2(cw_dp__1[3]), .pin3(cw_dp__1[4]), .pin4(ZERO), .pin5(ZERO), .pin6(cw_dp__1[5]),
    .pin7(z_dest_n[15]), .pin15(z_dest_n[8]), .pin14(z_dest_n[9]), .pin13(z_dest_n[10]),
    .pin12(z_dest_n[11]), .pin11(z_dest_n[12]), .pin10(z_dest_n[13]), .pin9(z_dest_n[14]));
  _74139 d2 (
    .pin1(ZERO), .pin2(cw_dp__0[30]), .pin3(cw_dp__0[31]), .pin4(cc_write_n[0]), .pin5(cc_write_n[1]),
    .pin6(cc_write_n[2]), .pin7(cc_write_n[3]), .pin15(ZERO), .pin14(cw_dp__1[0]), .pin13(cw_dp__1[1]),
    .pin12(cc_mi_n[0]), .pin11(cc_mi_n[1]), .pin10(cc_mi_n[2]), .pin9(cc_mi_n[3]));
  _74139 d6 (
    .pin1(ZERO), .pin2(cw_dp__1[18]), .pin3(cw_dp__1[19]), .pin4(mmu_addr_n[0]), .pin5(mmu_addr_n[1]),
    .pin6(mmu_addr_n[2]), .pin7(mmu_addr_n[3]), .pin15(ZERO), .pin14(cw_dp__1[20]), .pin13(cw_dp__1[21]),
    .pin12(mmu_map_n[0]), .pin11(mmu_map_n[1]), .pin10(mmu_map_n[2]), .pin9(mmu_map_n[3]));
  _74138 op_hi (
    .pin1(cw_dp__0[11]), .pin2(cw_dp__0[12]), .pin3(cw_dp__0[13]), .pin4(ZERO), .pin5(ZERO),
    .pin6(cw_dp__0[14]), .pin7(alu_op_n[15]), .pin15(alu_op_n[8]), .pin14(alu_op_n[9]), .pin13(alu_op_n[10]),
    .pin12(alu_op_n[11]), .pin11(alu_op_n[12]), .pin10(alu_op_n[13]), .pin9(alu_op_n[14]));
  _74138 zd_lo (
    .pin1(cw_dp__1[2]), .pin2(cw_dp__1[3]), .pin3(cw_dp__1[4]), .pin4(cw_dp__1[5]), .pin5(ZERO), .pin6(ONE),
    .pin7(z_dest_n[7]), .pin15(z_dest_n[0]), .pin14(z_dest_n[1]), .pin13(z_dest_n[2]), .pin12(z_dest_n[3]),
    .pin11(z_dest_n[4]), .pin10(z_dest_n[5]), .pin9(z_dest_n[6]));

  assign alu_cin = cw_dp__0[18];
  assign alu_width = cw_dp__0[19];
  assign flag_we = cw_dp__0[24:20];
  assign sp_bank = cw_dp__1[24];
  assign tas_lock = cw_dp__1[25];
  assign z_accum = cw_dp__0[29];
  // also tied to GND on the sheet: ZERO
  // also tied to VCC on the sheet: ONE
endmodule

module uc_loader (
  input  clk,
  input  rst_n,
  output [11:0] sram_addr,
  output [7:0] sram_wdata,
  output [12:0] cs_n,
  output loading
);

  wire ONE, ZERO;
  wire [3:0] rco;
  wire [7:6] dhi;
  wire [15:12] cnt;

  _74161 c0 (
    .pin1(rst_n), .pin2(clk), .pin3(ZERO), .pin4(ZERO), .pin5(ZERO), .pin6(ZERO), .pin7(loading),
    .pin15(rco[0]), .pin14(sram_addr[0]), .pin13(sram_addr[1]), .pin12(sram_addr[2]), .pin11(sram_addr[3]),
    .pin10(loading), .pin9(ONE));
  _74138 dec_hi (
    .pin1(cnt[12]), .pin2(cnt[13]), .pin3(cnt[14]), .pin4(ZERO), .pin5(ZERO), .pin6(cnt[15]), .pin7(dhi[7]),
    .pin15(cs_n[8]), .pin14(cs_n[9]), .pin13(cs_n[10]), .pin12(cs_n[11]), .pin11(cs_n[12]), .pin10(loading),
    .pin9(dhi[6]));
  _74161 c1 (
    .pin1(rst_n), .pin2(clk), .pin3(ZERO), .pin4(ZERO), .pin5(ZERO), .pin6(ZERO), .pin7(loading),
    .pin15(rco[1]), .pin14(sram_addr[4]), .pin13(sram_addr[5]), .pin12(sram_addr[6]), .pin11(sram_addr[7]),
    .pin10(rco[0]), .pin9(ONE));
  _74138 dec_lo (
    .pin1(cnt[12]), .pin2(cnt[13]), .pin3(cnt[14]), .pin4(cnt[15]), .pin5(ZERO), .pin6(ONE), .pin7(cs_n[7]),
    .pin15(cs_n[0]), .pin14(cs_n[1]), .pin13(cs_n[2]), .pin12(cs_n[3]), .pin11(cs_n[4]), .pin10(cs_n[5]),
    .pin9(cs_n[6]));
  _74161 c2 (
    .pin1(rst_n), .pin2(clk), .pin3(ZERO), .pin4(ZERO), .pin5(ZERO), .pin6(ZERO), .pin7(loading),
    .pin15(rco[2]), .pin14(sram_addr[8]), .pin13(sram_addr[9]), .pin12(sram_addr[10]), .pin11(sram_addr[11]),
    .pin10(rco[1]), .pin9(ONE));
  sst39sf010a eeprom (
    .a16(ZERO), .a15(cnt[15]), .a12(cnt[12]), .a7(sram_addr[7]), .a6(sram_addr[6]), .a5(sram_addr[5]),
    .a4(sram_addr[4]), .a3(sram_addr[3]), .a2(sram_addr[2]), .a1(sram_addr[1]), .a0(sram_addr[0]),
    .dq0(sram_wdata[0]), .dq1(sram_wdata[1]), .dq2(sram_wdata[2]), .dq3(sram_wdata[3]), .dq4(sram_wdata[4]),
    .dq5(sram_wdata[5]), .dq6(sram_wdata[6]), .dq7(sram_wdata[7]), .ce_n(ZERO), .a10(sram_addr[10]),
    .oe_n(ZERO), .a11(sram_addr[11]), .a9(sram_addr[9]), .a8(sram_addr[8]), .a13(cnt[13]), .a14(cnt[14]),
    .we_n(ONE));
  _74161 c3 (
    .pin1(rst_n), .pin2(clk), .pin3(ZERO), .pin4(ZERO), .pin5(ZERO), .pin6(ZERO), .pin7(loading),
    .pin15(rco[3]), .pin14(cnt[12]), .pin13(cnt[13]), .pin12(cnt[14]), .pin11(cnt[15]), .pin10(rco[2]),
    .pin9(ONE));
  // also tied to GND on the sheet: ZERO
  // also tied to VCC on the sheet: ONE

  // Other names for the same wires on the sheet: cnt[11:0] = sram_addr; dhi[5] = loading; rom_data[7:0] = sram_wdata
endmodule

module opcode_lut (
  input  clk,
  input  [11:0] loader_addr,
  input  dispatch_page,
  input  [7:0] ir,
  input  loading,
  input  [7:0] wdata,
  input  wbuf_oe_n,
  input  oe_n,
  input  [1:0] cs_n,
  output [7:0] lut_lo,
  output [7:0] lut_hi
);

  wire ZERO;
  wire [3:0] we_pad;
  wire [11:0] addr;

  _74157 a0 (
    .pin1(loading), .pin2(ir[0]), .pin3(loader_addr[0]), .pin4(addr[0]), .pin5(ir[1]), .pin6(loader_addr[1]),
    .pin7(addr[1]), .pin15(ZERO), .pin14(ir[3]), .pin13(loader_addr[3]), .pin12(addr[3]), .pin11(ir[2]),
    .pin10(loader_addr[2]), .pin9(addr[2]));
  _74541 chip_0__wbuf (
    .pin1(wbuf_oe_n), .pin2(wdata[0]), .pin3(wdata[1]), .pin4(wdata[2]), .pin5(wdata[3]), .pin6(wdata[4]),
    .pin7(wdata[5]), .pin8(wdata[6]), .pin9(wdata[7]), .pin19(ZERO), .pin18(lut_lo[0]), .pin17(lut_lo[1]),
    .pin16(lut_lo[2]), .pin15(lut_lo[3]), .pin14(lut_lo[4]), .pin13(lut_lo[5]), .pin12(lut_lo[6]),
    .pin11(lut_lo[7]));
  _74157 a1 (
    .pin1(loading), .pin2(ir[4]), .pin3(loader_addr[4]), .pin4(addr[4]), .pin5(ir[5]), .pin6(loader_addr[5]),
    .pin7(addr[5]), .pin15(ZERO), .pin14(ir[7]), .pin13(loader_addr[7]), .pin12(addr[7]), .pin11(ir[6]),
    .pin10(loader_addr[6]), .pin9(addr[6]));
  is61c64 chip_1__sram (
    .a12(ZERO), .a7(addr[7]), .a6(addr[6]), .a5(addr[5]), .a4(addr[4]), .a3(addr[3]), .a2(addr[2]),
    .a1(addr[1]), .a0(addr[0]), .io0(lut_hi[0]), .io1(lut_hi[1]), .io2(lut_hi[2]), .io3(lut_hi[3]),
    .io4(lut_hi[4]), .io5(lut_hi[5]), .io6(lut_hi[6]), .io7(lut_hi[7]), .ce_n(ZERO), .a10(addr[10]),
    .oe_n(oe_n), .a11(addr[11]), .a9(addr[9]), .a8(addr[8]), .we_n(we_pad[1]));
  _74157 a2 (
    .pin1(loading), .pin2(dispatch_page), .pin3(loader_addr[8]), .pin4(addr[8]), .pin5(ZERO),
    .pin6(loader_addr[9]), .pin7(addr[9]), .pin15(ZERO), .pin14(ZERO), .pin13(loader_addr[11]),
    .pin12(addr[11]), .pin11(ZERO), .pin10(loader_addr[10]), .pin9(addr[10]));
  _74541 chip_1__wbuf (
    .pin1(wbuf_oe_n), .pin2(wdata[0]), .pin3(wdata[1]), .pin4(wdata[2]), .pin5(wdata[3]), .pin6(wdata[4]),
    .pin7(wdata[5]), .pin8(wdata[6]), .pin9(wdata[7]), .pin19(ZERO), .pin18(lut_hi[0]), .pin17(lut_hi[1]),
    .pin16(lut_hi[2]), .pin15(lut_hi[3]), .pin14(lut_hi[4]), .pin13(lut_hi[5]), .pin12(lut_hi[6]),
    .pin11(lut_hi[7]));
  is61c64 chip_0__sram (
    .a12(ZERO), .a7(addr[7]), .a6(addr[6]), .a5(addr[5]), .a4(addr[4]), .a3(addr[3]), .a2(addr[2]),
    .a1(addr[1]), .a0(addr[0]), .io0(lut_lo[0]), .io1(lut_lo[1]), .io2(lut_lo[2]), .io3(lut_lo[3]),
    .io4(lut_lo[4]), .io5(lut_lo[5]), .io6(lut_lo[6]), .io7(lut_lo[7]), .ce_n(ZERO), .a10(addr[10]),
    .oe_n(oe_n), .a11(addr[11]), .a9(addr[9]), .a8(addr[8]), .we_n(we_pad[0]));
  _7432 ws (
    .pin1(cs_n[0]), .pin2(clk), .pin3(we_pad[0]), .pin4(cs_n[1]), .pin5(clk), .pin6(we_pad[1]), .pin13(clk),
    .pin12(ZERO), .pin11(we_pad[3]), .pin10(clk), .pin9(ZERO), .pin8(we_pad[2]));
  // also tied to GND on the sheet: ZERO

  // Other names for the same wires on the sheet: _0_io_0__7_0_[7:0] = lut_lo; _0_io_1__7_0_[7:0] = lut_hi;
  //   run_addr[8:0] = {dispatch_page, ir}
endmodule

module microcode_store (
  input  clk,
  input  [11:0] upc,
  input  [11:0] loader_addr,
  input  loading,
  input  [7:0] wdata,
  input  wbuf_oe_n,
  input  oe_n,
  input  [10:0] cs_n,
  output [31:0] cw__0,
  output [31:0] cw__1,
  output [23:0] cw__2
);

  wire ZERO;
  wire [11:0] addr, we_pad;

  _74157 a0 (
    .pin1(loading), .pin2(upc[0]), .pin3(loader_addr[0]), .pin4(addr[0]), .pin5(upc[1]),
    .pin6(loader_addr[1]), .pin7(addr[1]), .pin15(ZERO), .pin14(upc[3]), .pin13(loader_addr[3]),
    .pin12(addr[3]), .pin11(upc[2]), .pin10(loader_addr[2]), .pin9(addr[2]));
  _74541 chip_0__wbuf (
    .pin1(wbuf_oe_n), .pin2(wdata[0]), .pin3(wdata[1]), .pin4(wdata[2]), .pin5(wdata[3]), .pin6(wdata[4]),
    .pin7(wdata[5]), .pin8(wdata[6]), .pin9(wdata[7]), .pin19(ZERO), .pin18(cw__0[0]), .pin17(cw__0[1]),
    .pin16(cw__0[2]), .pin15(cw__0[3]), .pin14(cw__0[4]), .pin13(cw__0[5]), .pin12(cw__0[6]), .pin11(cw__0[7]));
  _74541 chip_1__wbuf (
    .pin1(wbuf_oe_n), .pin2(wdata[0]), .pin3(wdata[1]), .pin4(wdata[2]), .pin5(wdata[3]), .pin6(wdata[4]),
    .pin7(wdata[5]), .pin8(wdata[6]), .pin9(wdata[7]), .pin19(ZERO), .pin18(cw__0[8]), .pin17(cw__0[9]),
    .pin16(cw__0[10]), .pin15(cw__0[11]), .pin14(cw__0[12]), .pin13(cw__0[13]), .pin12(cw__0[14]),
    .pin11(cw__0[15]));
  _74541 chip_3__wbuf (
    .pin1(wbuf_oe_n), .pin2(wdata[0]), .pin3(wdata[1]), .pin4(wdata[2]), .pin5(wdata[3]), .pin6(wdata[4]),
    .pin7(wdata[5]), .pin8(wdata[6]), .pin9(wdata[7]), .pin19(ZERO), .pin18(cw__0[24]), .pin17(cw__0[25]),
    .pin16(cw__0[26]), .pin15(cw__0[27]), .pin14(cw__0[28]), .pin13(cw__0[29]), .pin12(cw__0[30]),
    .pin11(cw__0[31]));
  _74541 chip_5__wbuf (
    .pin1(wbuf_oe_n), .pin2(wdata[0]), .pin3(wdata[1]), .pin4(wdata[2]), .pin5(wdata[3]), .pin6(wdata[4]),
    .pin7(wdata[5]), .pin8(wdata[6]), .pin9(wdata[7]), .pin19(ZERO), .pin18(cw__1[8]), .pin17(cw__1[9]),
    .pin16(cw__1[10]), .pin15(cw__1[11]), .pin14(cw__1[12]), .pin13(cw__1[13]), .pin12(cw__1[14]),
    .pin11(cw__1[15]));
  _74541 chip_7__wbuf (
    .pin1(wbuf_oe_n), .pin2(wdata[0]), .pin3(wdata[1]), .pin4(wdata[2]), .pin5(wdata[3]), .pin6(wdata[4]),
    .pin7(wdata[5]), .pin8(wdata[6]), .pin9(wdata[7]), .pin19(ZERO), .pin18(cw__1[24]), .pin17(cw__1[25]),
    .pin16(cw__1[26]), .pin15(cw__1[27]), .pin14(cw__1[28]), .pin13(cw__1[29]), .pin12(cw__1[30]),
    .pin11(cw__1[31]));
  _74541 chip_9__wbuf (
    .pin1(wbuf_oe_n), .pin2(wdata[0]), .pin3(wdata[1]), .pin4(wdata[2]), .pin5(wdata[3]), .pin6(wdata[4]),
    .pin7(wdata[5]), .pin8(wdata[6]), .pin9(wdata[7]), .pin19(ZERO), .pin18(cw__2[8]), .pin17(cw__2[9]),
    .pin16(cw__2[10]), .pin15(cw__2[11]), .pin14(cw__2[12]), .pin13(cw__2[13]), .pin12(cw__2[14]),
    .pin11(cw__2[15]));
  _74157 a1 (
    .pin1(loading), .pin2(upc[4]), .pin3(loader_addr[4]), .pin4(addr[4]), .pin5(upc[5]),
    .pin6(loader_addr[5]), .pin7(addr[5]), .pin15(ZERO), .pin14(upc[7]), .pin13(loader_addr[7]),
    .pin12(addr[7]), .pin11(upc[6]), .pin10(loader_addr[6]), .pin9(addr[6]));
  is61c64 chip_10__sram (
    .a12(ZERO), .a7(addr[7]), .a6(addr[6]), .a5(addr[5]), .a4(addr[4]), .a3(addr[3]), .a2(addr[2]),
    .a1(addr[1]), .a0(addr[0]), .io0(cw__2[16]), .io1(cw__2[17]), .io2(cw__2[18]), .io3(cw__2[19]),
    .io4(cw__2[20]), .io5(cw__2[21]), .io6(cw__2[22]), .io7(cw__2[23]), .ce_n(ZERO), .a10(addr[10]),
    .oe_n(oe_n), .a11(addr[11]), .a9(addr[9]), .a8(addr[8]), .we_n(we_pad[10]));
  is61c64 chip_2__sram (
    .a12(ZERO), .a7(addr[7]), .a6(addr[6]), .a5(addr[5]), .a4(addr[4]), .a3(addr[3]), .a2(addr[2]),
    .a1(addr[1]), .a0(addr[0]), .io0(cw__0[16]), .io1(cw__0[17]), .io2(cw__0[18]), .io3(cw__0[19]),
    .io4(cw__0[20]), .io5(cw__0[21]), .io6(cw__0[22]), .io7(cw__0[23]), .ce_n(ZERO), .a10(addr[10]),
    .oe_n(oe_n), .a11(addr[11]), .a9(addr[9]), .a8(addr[8]), .we_n(we_pad[2]));
  is61c64 chip_4__sram (
    .a12(ZERO), .a7(addr[7]), .a6(addr[6]), .a5(addr[5]), .a4(addr[4]), .a3(addr[3]), .a2(addr[2]),
    .a1(addr[1]), .a0(addr[0]), .io0(cw__1[0]), .io1(cw__1[1]), .io2(cw__1[2]), .io3(cw__1[3]),
    .io4(cw__1[4]), .io5(cw__1[5]), .io6(cw__1[6]), .io7(cw__1[7]), .ce_n(ZERO), .a10(addr[10]), .oe_n(oe_n),
    .a11(addr[11]), .a9(addr[9]), .a8(addr[8]), .we_n(we_pad[4]));
  is61c64 chip_6__sram (
    .a12(ZERO), .a7(addr[7]), .a6(addr[6]), .a5(addr[5]), .a4(addr[4]), .a3(addr[3]), .a2(addr[2]),
    .a1(addr[1]), .a0(addr[0]), .io0(cw__1[16]), .io1(cw__1[17]), .io2(cw__1[18]), .io3(cw__1[19]),
    .io4(cw__1[20]), .io5(cw__1[21]), .io6(cw__1[22]), .io7(cw__1[23]), .ce_n(ZERO), .a10(addr[10]),
    .oe_n(oe_n), .a11(addr[11]), .a9(addr[9]), .a8(addr[8]), .we_n(we_pad[6]));
  is61c64 chip_8__sram (
    .a12(ZERO), .a7(addr[7]), .a6(addr[6]), .a5(addr[5]), .a4(addr[4]), .a3(addr[3]), .a2(addr[2]),
    .a1(addr[1]), .a0(addr[0]), .io0(cw__2[0]), .io1(cw__2[1]), .io2(cw__2[2]), .io3(cw__2[3]),
    .io4(cw__2[4]), .io5(cw__2[5]), .io6(cw__2[6]), .io7(cw__2[7]), .ce_n(ZERO), .a10(addr[10]), .oe_n(oe_n),
    .a11(addr[11]), .a9(addr[9]), .a8(addr[8]), .we_n(we_pad[8]));
  _7432 ws0 (
    .pin1(cs_n[0]), .pin2(clk), .pin3(we_pad[0]), .pin4(cs_n[1]), .pin5(clk), .pin6(we_pad[1]), .pin13(clk),
    .pin12(cs_n[3]), .pin11(we_pad[3]), .pin10(clk), .pin9(cs_n[2]), .pin8(we_pad[2]));
  _74157 a2 (
    .pin1(loading), .pin2(upc[8]), .pin3(loader_addr[8]), .pin4(addr[8]), .pin5(upc[9]),
    .pin6(loader_addr[9]), .pin7(addr[9]), .pin15(ZERO), .pin14(upc[11]), .pin13(loader_addr[11]),
    .pin12(addr[11]), .pin11(upc[10]), .pin10(loader_addr[10]), .pin9(addr[10]));
  _74541 chip_10__wbuf (
    .pin1(wbuf_oe_n), .pin2(wdata[0]), .pin3(wdata[1]), .pin4(wdata[2]), .pin5(wdata[3]), .pin6(wdata[4]),
    .pin7(wdata[5]), .pin8(wdata[6]), .pin9(wdata[7]), .pin19(ZERO), .pin18(cw__2[16]), .pin17(cw__2[17]),
    .pin16(cw__2[18]), .pin15(cw__2[19]), .pin14(cw__2[20]), .pin13(cw__2[21]), .pin12(cw__2[22]),
    .pin11(cw__2[23]));
  _74541 chip_2__wbuf (
    .pin1(wbuf_oe_n), .pin2(wdata[0]), .pin3(wdata[1]), .pin4(wdata[2]), .pin5(wdata[3]), .pin6(wdata[4]),
    .pin7(wdata[5]), .pin8(wdata[6]), .pin9(wdata[7]), .pin19(ZERO), .pin18(cw__0[16]), .pin17(cw__0[17]),
    .pin16(cw__0[18]), .pin15(cw__0[19]), .pin14(cw__0[20]), .pin13(cw__0[21]), .pin12(cw__0[22]),
    .pin11(cw__0[23]));
  _74541 chip_4__wbuf (
    .pin1(wbuf_oe_n), .pin2(wdata[0]), .pin3(wdata[1]), .pin4(wdata[2]), .pin5(wdata[3]), .pin6(wdata[4]),
    .pin7(wdata[5]), .pin8(wdata[6]), .pin9(wdata[7]), .pin19(ZERO), .pin18(cw__1[0]), .pin17(cw__1[1]),
    .pin16(cw__1[2]), .pin15(cw__1[3]), .pin14(cw__1[4]), .pin13(cw__1[5]), .pin12(cw__1[6]), .pin11(cw__1[7]));
  _74541 chip_6__wbuf (
    .pin1(wbuf_oe_n), .pin2(wdata[0]), .pin3(wdata[1]), .pin4(wdata[2]), .pin5(wdata[3]), .pin6(wdata[4]),
    .pin7(wdata[5]), .pin8(wdata[6]), .pin9(wdata[7]), .pin19(ZERO), .pin18(cw__1[16]), .pin17(cw__1[17]),
    .pin16(cw__1[18]), .pin15(cw__1[19]), .pin14(cw__1[20]), .pin13(cw__1[21]), .pin12(cw__1[22]),
    .pin11(cw__1[23]));
  _74541 chip_8__wbuf (
    .pin1(wbuf_oe_n), .pin2(wdata[0]), .pin3(wdata[1]), .pin4(wdata[2]), .pin5(wdata[3]), .pin6(wdata[4]),
    .pin7(wdata[5]), .pin8(wdata[6]), .pin9(wdata[7]), .pin19(ZERO), .pin18(cw__2[0]), .pin17(cw__2[1]),
    .pin16(cw__2[2]), .pin15(cw__2[3]), .pin14(cw__2[4]), .pin13(cw__2[5]), .pin12(cw__2[6]), .pin11(cw__2[7]));
  _7432 ws1 (
    .pin1(cs_n[4]), .pin2(clk), .pin3(we_pad[4]), .pin4(cs_n[5]), .pin5(clk), .pin6(we_pad[5]), .pin13(clk),
    .pin12(cs_n[7]), .pin11(we_pad[7]), .pin10(clk), .pin9(cs_n[6]), .pin8(we_pad[6]));
  is61c64 chip_0__sram (
    .a12(ZERO), .a7(addr[7]), .a6(addr[6]), .a5(addr[5]), .a4(addr[4]), .a3(addr[3]), .a2(addr[2]),
    .a1(addr[1]), .a0(addr[0]), .io0(cw__0[0]), .io1(cw__0[1]), .io2(cw__0[2]), .io3(cw__0[3]),
    .io4(cw__0[4]), .io5(cw__0[5]), .io6(cw__0[6]), .io7(cw__0[7]), .ce_n(ZERO), .a10(addr[10]), .oe_n(oe_n),
    .a11(addr[11]), .a9(addr[9]), .a8(addr[8]), .we_n(we_pad[0]));
  is61c64 chip_1__sram (
    .a12(ZERO), .a7(addr[7]), .a6(addr[6]), .a5(addr[5]), .a4(addr[4]), .a3(addr[3]), .a2(addr[2]),
    .a1(addr[1]), .a0(addr[0]), .io0(cw__0[8]), .io1(cw__0[9]), .io2(cw__0[10]), .io3(cw__0[11]),
    .io4(cw__0[12]), .io5(cw__0[13]), .io6(cw__0[14]), .io7(cw__0[15]), .ce_n(ZERO), .a10(addr[10]),
    .oe_n(oe_n), .a11(addr[11]), .a9(addr[9]), .a8(addr[8]), .we_n(we_pad[1]));
  is61c64 chip_3__sram (
    .a12(ZERO), .a7(addr[7]), .a6(addr[6]), .a5(addr[5]), .a4(addr[4]), .a3(addr[3]), .a2(addr[2]),
    .a1(addr[1]), .a0(addr[0]), .io0(cw__0[24]), .io1(cw__0[25]), .io2(cw__0[26]), .io3(cw__0[27]),
    .io4(cw__0[28]), .io5(cw__0[29]), .io6(cw__0[30]), .io7(cw__0[31]), .ce_n(ZERO), .a10(addr[10]),
    .oe_n(oe_n), .a11(addr[11]), .a9(addr[9]), .a8(addr[8]), .we_n(we_pad[3]));
  is61c64 chip_5__sram (
    .a12(ZERO), .a7(addr[7]), .a6(addr[6]), .a5(addr[5]), .a4(addr[4]), .a3(addr[3]), .a2(addr[2]),
    .a1(addr[1]), .a0(addr[0]), .io0(cw__1[8]), .io1(cw__1[9]), .io2(cw__1[10]), .io3(cw__1[11]),
    .io4(cw__1[12]), .io5(cw__1[13]), .io6(cw__1[14]), .io7(cw__1[15]), .ce_n(ZERO), .a10(addr[10]),
    .oe_n(oe_n), .a11(addr[11]), .a9(addr[9]), .a8(addr[8]), .we_n(we_pad[5]));
  is61c64 chip_7__sram (
    .a12(ZERO), .a7(addr[7]), .a6(addr[6]), .a5(addr[5]), .a4(addr[4]), .a3(addr[3]), .a2(addr[2]),
    .a1(addr[1]), .a0(addr[0]), .io0(cw__1[24]), .io1(cw__1[25]), .io2(cw__1[26]), .io3(cw__1[27]),
    .io4(cw__1[28]), .io5(cw__1[29]), .io6(cw__1[30]), .io7(cw__1[31]), .ce_n(ZERO), .a10(addr[10]),
    .oe_n(oe_n), .a11(addr[11]), .a9(addr[9]), .a8(addr[8]), .we_n(we_pad[7]));
  is61c64 chip_9__sram (
    .a12(ZERO), .a7(addr[7]), .a6(addr[6]), .a5(addr[5]), .a4(addr[4]), .a3(addr[3]), .a2(addr[2]),
    .a1(addr[1]), .a0(addr[0]), .io0(cw__2[8]), .io1(cw__2[9]), .io2(cw__2[10]), .io3(cw__2[11]),
    .io4(cw__2[12]), .io5(cw__2[13]), .io6(cw__2[14]), .io7(cw__2[15]), .ce_n(ZERO), .a10(addr[10]),
    .oe_n(oe_n), .a11(addr[11]), .a9(addr[9]), .a8(addr[8]), .we_n(we_pad[9]));
  _7432 ws2 (
    .pin1(cs_n[8]), .pin2(clk), .pin3(we_pad[8]), .pin4(cs_n[9]), .pin5(clk), .pin6(we_pad[9]), .pin13(clk),
    .pin12(ZERO), .pin11(we_pad[11]), .pin10(clk), .pin9(cs_n[10]), .pin8(we_pad[10]));
  // also tied to GND on the sheet: ZERO
endmodule

module microsequencer (
  input  clk,
  input  clr_n,
  input  [2:0] useq_op,
  input  [11:0] next_addr,
  input  [3:0] ucond_sel,
  input  ucond_pol,
  input  [15:0] cond,
  input  [11:0] lut_data,
  output [11:0] upc
);

  wire cond_hi, cond_lo, ONE, ZERO;
  wire [2:0] upc_rco;
  wire [3:0] and_y, merge_y, or_y, xor_y;
  wire [4:4] inv_a;
  wire [5:0] inv_y;
  wire [7:0] op_n;
  wire [11:0] p;

  _7408 brand (
    .pin1(inv_y[0]), .pin2(xor_y[0]), .pin3(and_y[0]), .pin4(ZERO), .pin5(ZERO), .pin6(and_y[1]),
    .pin13(ZERO), .pin12(ZERO), .pin11(and_y[3]), .pin10(ZERO), .pin9(ZERO), .pin8(and_y[2]));
  _7486 cpol (
    .pin1(merge_y[0]), .pin2(ucond_pol), .pin3(xor_y[0]), .pin4(ZERO), .pin5(ZERO), .pin6(xor_y[1]),
    .pin13(ZERO), .pin12(ZERO), .pin11(xor_y[3]), .pin10(ZERO), .pin9(ZERO), .pin8(xor_y[2]));
  _74153 nmux_1__m (
    .pin1(ZERO), .pin2(inv_y[3]), .pin3(ZERO), .pin4(ZERO), .pin5(lut_data[2]), .pin6(next_addr[2]),
    .pin7(p[2]), .pin15(inv_y[2]), .pin14(ZERO), .pin13(ZERO), .pin12(ZERO), .pin11(lut_data[3]),
    .pin10(next_addr[3]), .pin9(p[3]));
  _74153 nmux_5__m (
    .pin1(ZERO), .pin2(inv_y[3]), .pin3(ZERO), .pin4(ZERO), .pin5(lut_data[10]), .pin6(next_addr[10]),
    .pin7(p[10]), .pin15(inv_y[2]), .pin14(ZERO), .pin13(ZERO), .pin12(ZERO), .pin11(lut_data[11]),
    .pin10(next_addr[11]), .pin9(p[11]));
  _74138 useq (
    .pin1(useq_op[0]), .pin2(useq_op[1]), .pin3(useq_op[2]), .pin4(ZERO), .pin5(ZERO), .pin6(ONE),
    .pin7(op_n[7]), .pin15(op_n[0]), .pin14(op_n[1]), .pin13(op_n[2]), .pin12(op_n[3]), .pin11(op_n[4]),
    .pin10(op_n[5]), .pin9(op_n[6]));
  _74157 cmerge (
    .pin1(ucond_sel[3]), .pin2(cond_lo), .pin3(cond_hi), .pin4(merge_y[0]), .pin5(ZERO), .pin6(ZERO),
    .pin7(merge_y[1]), .pin15(ZERO), .pin14(ZERO), .pin13(ZERO), .pin12(merge_y[3]), .pin11(ZERO),
    .pin10(ZERO), .pin9(merge_y[2]));
  _7404 inv (
    .pin1(op_n[1]), .pin2(inv_y[0]), .pin3(op_n[2]), .pin4(inv_y[1]), .pin5(op_n[3]), .pin6(inv_y[2]),
    .pin13(ZERO), .pin12(inv_y[5]), .pin11(inv_a[4]), .pin10(inv_y[4]), .pin9(op_n[4]), .pin8(inv_y[3]));
  _74153 nmux_2__m (
    .pin1(ZERO), .pin2(inv_y[3]), .pin3(ZERO), .pin4(ZERO), .pin5(lut_data[4]), .pin6(next_addr[4]),
    .pin7(p[4]), .pin15(inv_y[2]), .pin14(ZERO), .pin13(ZERO), .pin12(ZERO), .pin11(lut_data[5]),
    .pin10(next_addr[5]), .pin9(p[5]));
  _74161 u0 (
    .pin1(clr_n), .pin2(clk), .pin3(p[0]), .pin4(p[1]), .pin5(p[2]), .pin6(p[3]), .pin7(op_n[5]),
    .pin15(upc_rco[0]), .pin14(upc[0]), .pin13(upc[1]), .pin12(upc[2]), .pin11(upc[3]), .pin10(op_n[5]),
    .pin9(inv_y[4]));
  _74151 cmux_hi (
    .pin1(cond[11]), .pin2(cond[10]), .pin3(cond[9]), .pin4(cond[8]), .pin5(cond_hi), .pin7(ZERO),
    .pin15(cond[12]), .pin14(cond[13]), .pin13(cond[14]), .pin12(cond[15]), .pin11(ucond_sel[0]),
    .pin10(ucond_sel[1]), .pin9(ucond_sel[2]));  // open: pin6
  _7432 lor (
    .pin1(inv_y[1]), .pin2(and_y[0]), .pin3(or_y[0]), .pin4(inv_y[2]), .pin5(inv_y[3]), .pin6(or_y[1]),
    .pin13(ZERO), .pin12(ZERO), .pin11(or_y[3]), .pin10(or_y[1]), .pin9(or_y[0]), .pin8(inv_a[4]));
  _74153 nmux_3__m (
    .pin1(ZERO), .pin2(inv_y[3]), .pin3(ZERO), .pin4(ZERO), .pin5(lut_data[6]), .pin6(next_addr[6]),
    .pin7(p[6]), .pin15(inv_y[2]), .pin14(ZERO), .pin13(ZERO), .pin12(ZERO), .pin11(lut_data[7]),
    .pin10(next_addr[7]), .pin9(p[7]));
  _74161 u1 (
    .pin1(clr_n), .pin2(clk), .pin3(p[4]), .pin4(p[5]), .pin5(p[6]), .pin6(p[7]), .pin7(op_n[5]),
    .pin15(upc_rco[1]), .pin14(upc[4]), .pin13(upc[5]), .pin12(upc[6]), .pin11(upc[7]), .pin10(upc_rco[0]),
    .pin9(inv_y[4]));
  _74151 cmux_lo (
    .pin1(cond[3]), .pin2(cond[2]), .pin3(cond[1]), .pin4(cond[0]), .pin5(cond_lo), .pin7(ZERO),
    .pin15(cond[4]), .pin14(cond[5]), .pin13(cond[6]), .pin12(ONE), .pin11(ucond_sel[0]),
    .pin10(ucond_sel[1]), .pin9(ucond_sel[2]));  // open: pin6
  _74153 nmux_0__m (
    .pin1(ZERO), .pin2(inv_y[3]), .pin3(ZERO), .pin4(ZERO), .pin5(lut_data[0]), .pin6(next_addr[0]),
    .pin7(p[0]), .pin15(inv_y[2]), .pin14(ZERO), .pin13(ZERO), .pin12(ZERO), .pin11(lut_data[1]),
    .pin10(next_addr[1]), .pin9(p[1]));
  _74153 nmux_4__m (
    .pin1(ZERO), .pin2(inv_y[3]), .pin3(ZERO), .pin4(ZERO), .pin5(lut_data[8]), .pin6(next_addr[8]),
    .pin7(p[8]), .pin15(inv_y[2]), .pin14(ZERO), .pin13(ZERO), .pin12(ZERO), .pin11(lut_data[9]),
    .pin10(next_addr[9]), .pin9(p[9]));
  _74161 u2 (
    .pin1(clr_n), .pin2(clk), .pin3(p[8]), .pin4(p[9]), .pin5(p[10]), .pin6(p[11]), .pin7(op_n[5]),
    .pin15(upc_rco[2]), .pin14(upc[8]), .pin13(upc[9]), .pin12(upc[10]), .pin11(upc[11]), .pin10(upc_rco[1]),
    .pin9(inv_y[4]));
  // also tied to GND on the sheet: ZERO
  // also tied to VCC on the sheet: ONE
endmodule

module cpu (
  input  clk,
  input  rst_n,
  input  [7:0] ir_drive,
  input  [15:0] cond_drive,
  output loading,
  output [11:0] upc,
  output [31:0] cw__0,
  output [31:0] cw__1,
  output [23:0] cw__2,
  output [11:0] lut_out
);

  wire cs_sel_n_0, cs_sel_n_1, cs_sel_n_2, cs_sel_n_3, cs_sel_n_4, cs_sel_n_5, cs_sel_n_6, cs_sel_n_7,
       cs_sel_n_8, cs_sel_n_9, cs_sel_n_10, cs_sel_n_11, cs_sel_n_12, inv_y_0, inv_y_1, inv_y_2, inv_y_3,
       inv_y_4, inv_y_5, ir_0, ir_1, ir_2, ir_3, ir_4, ir_5, ir_6, ir_7, loader_addr_0, loader_addr_1,
       loader_addr_2, loader_addr_3, loader_addr_4, loader_addr_5, loader_addr_6, loader_addr_7,
       loader_addr_8, loader_addr_9, loader_addr_10, loader_addr_11, loader_wdata_0, loader_wdata_1,
       loader_wdata_2, loader_wdata_3, loader_wdata_4, loader_wdata_5, loader_wdata_6, loader_wdata_7,
       lut_hi_4, lut_hi_5, lut_hi_6, lut_hi_7, ZERO;

  _7404 inv (
    .pin1(loading), .pin2(inv_y_0), .pin3(ZERO), .pin4(inv_y_1), .pin5(ZERO), .pin6(inv_y_2), .pin13(ZERO),
    .pin12(inv_y_5), .pin11(ZERO), .pin10(inv_y_4), .pin9(ZERO), .pin8(inv_y_3));
  control_word_decoder dec (
    .cw_dp__0({cw__1[23:0], cw__0[31:24]}), .cw_dp__1({cw__2, cw__1[31:24]}));  // open: ir_load_n, left_src_n, left_lane_n, right_src_n, alu_op_n, alu_shift_n, v_src_n, c_src_n, cc_write_n, cc_mi_n, z_dest_n, z_lane_n, pc_ctrl_n, mar_ctrl_n, x_ctrl_n, y_ctrl_n, mem_op_n, mmu_addr_n, mmu_map_n, mmu_pt_n, alu_cin, alu_width, flag_we, z_accum, sp_bank, tas_lock
  microcode_store store (
    .clk(clk), .upc(upc),
    .loader_addr({loader_addr_11, loader_addr_10, loader_addr_9, loader_addr_8, loader_addr_7, loader_addr_6, loader_addr_5, loader_addr_4, loader_addr_3, loader_addr_2, loader_addr_1, loader_addr_0}),
    .loading(loading),
    .wdata({loader_wdata_7, loader_wdata_6, loader_wdata_5, loader_wdata_4, loader_wdata_3, loader_wdata_2, loader_wdata_1, loader_wdata_0}),
    .wbuf_oe_n(inv_y_0), .oe_n(loading),
    .cs_n({cs_sel_n_10, cs_sel_n_9, cs_sel_n_8, cs_sel_n_7, cs_sel_n_6, cs_sel_n_5, cs_sel_n_4, cs_sel_n_3, cs_sel_n_2, cs_sel_n_1, cs_sel_n_0}),
    .cw__0(cw__0), .cw__1(cw__1), .cw__2(cw__2));
  _74574 ir_reg (
    .OE_n(ZERO), .D0(ir_drive[0]), .D1(ir_drive[1]), .D2(ir_drive[2]), .D3(ir_drive[3]), .D4(ir_drive[4]),
    .D5(ir_drive[5]), .D6(ir_drive[6]), .D7(ir_drive[7]), .CLK(clk), .Q7(ir_7), .Q6(ir_6), .Q5(ir_5),
    .Q4(ir_4), .Q3(ir_3), .Q2(ir_2), .Q1(ir_1), .Q0(ir_0));
  uc_loader loader (
    .clk(clk), .rst_n(rst_n),
    .sram_addr({loader_addr_11, loader_addr_10, loader_addr_9, loader_addr_8, loader_addr_7, loader_addr_6, loader_addr_5, loader_addr_4, loader_addr_3, loader_addr_2, loader_addr_1, loader_addr_0}),
    .sram_wdata({loader_wdata_7, loader_wdata_6, loader_wdata_5, loader_wdata_4, loader_wdata_3, loader_wdata_2, loader_wdata_1, loader_wdata_0}),
    .cs_n({cs_sel_n_12, cs_sel_n_11, cs_sel_n_10, cs_sel_n_9, cs_sel_n_8, cs_sel_n_7, cs_sel_n_6, cs_sel_n_5, cs_sel_n_4, cs_sel_n_3, cs_sel_n_2, cs_sel_n_1, cs_sel_n_0}),
    .loading(loading));
  microsequencer useq (
    .clk(clk), .clr_n(inv_y_0), .useq_op(cw__0[2:0]), .next_addr(cw__0[14:3]), .ucond_sel(cw__0[18:15]),
    .ucond_pol(cw__0[19]), .cond(cond_drive), .lut_data(lut_out), .upc(upc));
  opcode_lut lut (
    .clk(clk),
    .loader_addr({loader_addr_11, loader_addr_10, loader_addr_9, loader_addr_8, loader_addr_7, loader_addr_6, loader_addr_5, loader_addr_4, loader_addr_3, loader_addr_2, loader_addr_1, loader_addr_0}),
    .dispatch_page(cw__0[22]), .ir({ir_7, ir_6, ir_5, ir_4, ir_3, ir_2, ir_1, ir_0}), .loading(loading),
    .wdata({loader_wdata_7, loader_wdata_6, loader_wdata_5, loader_wdata_4, loader_wdata_3, loader_wdata_2, loader_wdata_1, loader_wdata_0}),
    .wbuf_oe_n(inv_y_0), .oe_n(loading), .cs_n({cs_sel_n_12, cs_sel_n_11}), .lut_lo(lut_out[7:0]),
    .lut_hi({lut_hi_7, lut_hi_6, lut_hi_5, lut_hi_4, lut_out[11:8]}));
  // also tied to GND on the sheet: ZERO

  // Other names for the same wires on the sheet: net_fanin_4[12:0] = {cs_sel_n_12, cs_sel_n_11, cs_sel_n_10, cs_sel_n_9, cs_sel_n_8, cs_sel_n_7, cs_sel_n_6, cs_sel_n_5, cs_sel_n_4, cs_sel_n_3, cs_sel_n_2, cs_sel_n_1, cs_sel_n_0};
  //   net_fanin_8[1:0] = {cs_sel_n_12, cs_sel_n_11};
  //   net_fanin_2[11:0] = {loader_addr_11, loader_addr_10, loader_addr_9, loader_addr_8, loader_addr_7, loader_addr_6, loader_addr_5, loader_addr_4, loader_addr_3, loader_addr_2, loader_addr_1, loader_addr_0};
  //   net_fanin_5[11:0] = {loader_addr_11, loader_addr_10, loader_addr_9, loader_addr_8, loader_addr_7, loader_addr_6, loader_addr_5, loader_addr_4, loader_addr_3, loader_addr_2, loader_addr_1, loader_addr_0};
  //   net_fanin_12[11:0] = {loader_addr_11, loader_addr_10, loader_addr_9, loader_addr_8, loader_addr_7, loader_addr_6, loader_addr_5, loader_addr_4, loader_addr_3, loader_addr_2, loader_addr_1, loader_addr_0};
  //   net_fanin_6[7:0] = {ir_7, ir_6, ir_5, ir_4, ir_3, ir_2, ir_1, ir_0};
  //   net_fanin_3[7:0] = {loader_wdata_7, loader_wdata_6, loader_wdata_5, loader_wdata_4, loader_wdata_3, loader_wdata_2, loader_wdata_1, loader_wdata_0};
  //   net_fanin_7[7:0] = {loader_wdata_7, loader_wdata_6, loader_wdata_5, loader_wdata_4, loader_wdata_3, loader_wdata_2, loader_wdata_1, loader_wdata_0};
  //   net_fanin_13[7:0] = {loader_wdata_7, loader_wdata_6, loader_wdata_5, loader_wdata_4, loader_wdata_3, loader_wdata_2, loader_wdata_1, loader_wdata_0};
  //   net_fanin_10[7:0] = {lut_hi_7, lut_hi_6, lut_hi_5, lut_hi_4, lut_out[11:8]};
  //   net_fanin_14[10:0] = {cs_sel_n_10, cs_sel_n_9, cs_sel_n_8, cs_sel_n_7, cs_sel_n_6, cs_sel_n_5, cs_sel_n_4, cs_sel_n_3, cs_sel_n_2, cs_sel_n_1, cs_sel_n_0};
  //   cw_0 = cw__0[0]; net_fanin_15[31:0] = cw__0; net_fanin_18[2:0] = cw__0[2:0]; net_fanin_27[31:0] = cw__0;
  //   cw_1 = cw__0[1]; cw_2 = cw__0[2]; cw_3 = cw__0[3]; net_fanin_19[11:0] = cw__0[14:3]; cw_4 = cw__0[4];
  //   cw_5 = cw__0[5]; cw_6 = cw__0[6]; cw_7 = cw__0[7]; cw_8 = cw__0[8]; cw_9 = cw__0[9]; cw_10 = cw__0[10];
  //   cw_11 = cw__0[11]; cw_12 = cw__0[12]; cw_13 = cw__0[13]; cw_14 = cw__0[14]; cw_15 = cw__0[15];
  //   net_fanin_20[3:0] = cw__0[18:15]; cw_16 = cw__0[16]; cw_17 = cw__0[17]; cw_18 = cw__0[18]; cw_19 = cw__0[19];
  //   cw_20 = cw__0[20]; cw_21 = cw__0[21]; cw_22 = cw__0[22]; cw_23 = cw__0[23]; cw_24 = cw__0[24];
  //   net_fanin_0[31:0] = {cw__1[23:0], cw__0[31:24]}; cw_25 = cw__0[25]; cw_26 = cw__0[26]; cw_27 = cw__0[27];
  //   cw_28 = cw__0[28]; cw_29 = cw__0[29]; cw_30 = cw__0[30]; cw_31 = cw__0[31]; cond_drive_0 = cond_drive[0];
  //   net_fanin_21[15:0] = cond_drive; net_fanin_25[15:0] = cond_drive; cond_drive_1 = cond_drive[1];
  //   cond_drive_2 = cond_drive[2]; cond_drive_3 = cond_drive[3]; cond_drive_4 = cond_drive[4];
  //   cond_drive_5 = cond_drive[5]; cond_drive_6 = cond_drive[6]; cond_drive_7 = cond_drive[7];
  //   cond_drive_8 = cond_drive[8]; cond_drive_9 = cond_drive[9]; cond_drive_10 = cond_drive[10];
  //   cond_drive_11 = cond_drive[11]; cond_drive_12 = cond_drive[12]; cond_drive_13 = cond_drive[13];
  //   cond_drive_14 = cond_drive[14]; cond_drive_15 = cond_drive[15]; net_fanin_11[11:0] = upc;
  //   net_fanin_23[11:0] = upc; net_fanin_26[11:0] = upc; upc_0 = upc[0]; upc_1 = upc[1]; upc_2 = upc[2];
  //   upc_3 = upc[3]; upc_4 = upc[4]; upc_5 = upc[5]; upc_6 = upc[6]; upc_7 = upc[7]; upc_8 = upc[8]; upc_9 = upc[9];
  //   upc_10 = upc[10]; upc_11 = upc[11]; ir_drive_0 = ir_drive[0]; net_fanin_24[7:0] = ir_drive;
  //   ir_drive_1 = ir_drive[1]; ir_drive_2 = ir_drive[2]; ir_drive_3 = ir_drive[3]; ir_drive_4 = ir_drive[4];
  //   ir_drive_5 = ir_drive[5]; ir_drive_6 = ir_drive[6]; ir_drive_7 = ir_drive[7]; cw_32 = cw__1[0];
  //   net_fanin_16[31:0] = cw__1; net_fanin_28[31:0] = cw__1; cw_33 = cw__1[1]; cw_34 = cw__1[2]; cw_35 = cw__1[3];
  //   cw_36 = cw__1[4]; cw_37 = cw__1[5]; cw_38 = cw__1[6]; cw_39 = cw__1[7]; cw_40 = cw__1[8]; cw_41 = cw__1[9];
  //   cw_42 = cw__1[10]; cw_43 = cw__1[11]; cw_44 = cw__1[12]; cw_45 = cw__1[13]; cw_46 = cw__1[14];
  //   cw_47 = cw__1[15]; cw_48 = cw__1[16]; cw_49 = cw__1[17]; cw_50 = cw__1[18]; cw_51 = cw__1[19];
  //   cw_52 = cw__1[20]; cw_53 = cw__1[21]; cw_54 = cw__1[22]; cw_55 = cw__1[23]; cw_56 = cw__1[24];
  //   net_fanin_1[31:0] = {cw__2, cw__1[31:24]}; cw_57 = cw__1[25]; cw_58 = cw__1[26]; cw_59 = cw__1[27];
  //   cw_60 = cw__1[28]; cw_61 = cw__1[29]; cw_62 = cw__1[30]; cw_63 = cw__1[31]; cw_64 = cw__2[0];
  //   net_fanin_17[23:0] = cw__2; net_fanin_29[23:0] = cw__2; cw_65 = cw__2[1]; cw_66 = cw__2[2]; cw_67 = cw__2[3];
  //   cw_68 = cw__2[4]; cw_69 = cw__2[5]; cw_70 = cw__2[6]; cw_71 = cw__2[7]; cw_72 = cw__2[8]; cw_73 = cw__2[9];
  //   cw_74 = cw__2[10]; cw_75 = cw__2[11]; cw_76 = cw__2[12]; cw_77 = cw__2[13]; cw_78 = cw__2[14];
  //   cw_79 = cw__2[15]; cw_80 = cw__2[16]; cw_81 = cw__2[17]; cw_82 = cw__2[18]; cw_83 = cw__2[19];
  //   cw_84 = cw__2[20]; cw_85 = cw__2[21]; cw_86 = cw__2[22]; cw_87 = cw__2[23]; lut_data_0 = lut_out[0];
  //   net_fanin_9[7:0] = lut_out[7:0]; net_fanin_22[11:0] = lut_out; net_fanin_30[11:0] = lut_out;
  //   lut_data_1 = lut_out[1]; lut_data_2 = lut_out[2]; lut_data_3 = lut_out[3]; lut_data_4 = lut_out[4];
  //   lut_data_5 = lut_out[5]; lut_data_6 = lut_out[6]; lut_data_7 = lut_out[7]; lut_data_8 = lut_out[8];
  //   lut_data_9 = lut_out[9]; lut_data_10 = lut_out[10]; lut_data_11 = lut_out[11]
endmodule
