// Logisim project microcode_store.circ as structural Verilog: 2 circuits, main circuit microcode_store
module is61c64 (
  input  a12,
  input  a7,
  input  a6,
  input  a5,
  input  a4,
  input  a3,
  input  a2,
  input  a1,
  input  a0,
  input  ce_n,
  input  a10,
  input  oe_n,
  input  a11,
  input  a9,
  input  a8,
  input  we_n,
  output io0,
  output io1,
  output io2,
  output io3,
  output io4,
  output io5,
  output io6,
  output io7
);
endmodule

module microcode_store (
  input  clk,
  input  [11:0] upc,
  input  [11:0] loader_addr,
  input  loading,
  input  [7:0] wdata,
  input  wbuf_oe_n,
  input  oe_n,
  input  [10:0] cs_n,
  output [31:0] cw__0,
  output [31:0] cw__1,
  output [23:0] cw__2
);

  wire ZERO;
  wire [11:0] addr, we_pad;

  _74157 a0 (
    .pin1(loading), .pin2(upc[0]), .pin3(loader_addr[0]), .pin4(addr[0]), .pin5(upc[1]),
    .pin6(loader_addr[1]), .pin7(addr[1]), .pin15(ZERO), .pin14(upc[3]), .pin13(loader_addr[3]),
    .pin12(addr[3]), .pin11(upc[2]), .pin10(loader_addr[2]), .pin9(addr[2]));
  _74541 chip_0__wbuf (
    .pin1(wbuf_oe_n), .pin2(wdata[0]), .pin3(wdata[1]), .pin4(wdata[2]), .pin5(wdata[3]), .pin6(wdata[4]),
    .pin7(wdata[5]), .pin8(wdata[6]), .pin9(wdata[7]), .pin19(ZERO), .pin18(cw__0[0]), .pin17(cw__0[1]),
    .pin16(cw__0[2]), .pin15(cw__0[3]), .pin14(cw__0[4]), .pin13(cw__0[5]), .pin12(cw__0[6]), .pin11(cw__0[7]));
  _74541 chip_1__wbuf (
    .pin1(wbuf_oe_n), .pin2(wdata[0]), .pin3(wdata[1]), .pin4(wdata[2]), .pin5(wdata[3]), .pin6(wdata[4]),
    .pin7(wdata[5]), .pin8(wdata[6]), .pin9(wdata[7]), .pin19(ZERO), .pin18(cw__0[8]), .pin17(cw__0[9]),
    .pin16(cw__0[10]), .pin15(cw__0[11]), .pin14(cw__0[12]), .pin13(cw__0[13]), .pin12(cw__0[14]),
    .pin11(cw__0[15]));
  _74541 chip_3__wbuf (
    .pin1(wbuf_oe_n), .pin2(wdata[0]), .pin3(wdata[1]), .pin4(wdata[2]), .pin5(wdata[3]), .pin6(wdata[4]),
    .pin7(wdata[5]), .pin8(wdata[6]), .pin9(wdata[7]), .pin19(ZERO), .pin18(cw__0[24]), .pin17(cw__0[25]),
    .pin16(cw__0[26]), .pin15(cw__0[27]), .pin14(cw__0[28]), .pin13(cw__0[29]), .pin12(cw__0[30]),
    .pin11(cw__0[31]));
  _74541 chip_5__wbuf (
    .pin1(wbuf_oe_n), .pin2(wdata[0]), .pin3(wdata[1]), .pin4(wdata[2]), .pin5(wdata[3]), .pin6(wdata[4]),
    .pin7(wdata[5]), .pin8(wdata[6]), .pin9(wdata[7]), .pin19(ZERO), .pin18(cw__1[8]), .pin17(cw__1[9]),
    .pin16(cw__1[10]), .pin15(cw__1[11]), .pin14(cw__1[12]), .pin13(cw__1[13]), .pin12(cw__1[14]),
    .pin11(cw__1[15]));
  _74541 chip_7__wbuf (
    .pin1(wbuf_oe_n), .pin2(wdata[0]), .pin3(wdata[1]), .pin4(wdata[2]), .pin5(wdata[3]), .pin6(wdata[4]),
    .pin7(wdata[5]), .pin8(wdata[6]), .pin9(wdata[7]), .pin19(ZERO), .pin18(cw__1[24]), .pin17(cw__1[25]),
    .pin16(cw__1[26]), .pin15(cw__1[27]), .pin14(cw__1[28]), .pin13(cw__1[29]), .pin12(cw__1[30]),
    .pin11(cw__1[31]));
  _74541 chip_9__wbuf (
    .pin1(wbuf_oe_n), .pin2(wdata[0]), .pin3(wdata[1]), .pin4(wdata[2]), .pin5(wdata[3]), .pin6(wdata[4]),
    .pin7(wdata[5]), .pin8(wdata[6]), .pin9(wdata[7]), .pin19(ZERO), .pin18(cw__2[8]), .pin17(cw__2[9]),
    .pin16(cw__2[10]), .pin15(cw__2[11]), .pin14(cw__2[12]), .pin13(cw__2[13]), .pin12(cw__2[14]),
    .pin11(cw__2[15]));
  _74157 a1 (
    .pin1(loading), .pin2(upc[4]), .pin3(loader_addr[4]), .pin4(addr[4]), .pin5(upc[5]),
    .pin6(loader_addr[5]), .pin7(addr[5]), .pin15(ZERO), .pin14(upc[7]), .pin13(loader_addr[7]),
    .pin12(addr[7]), .pin11(upc[6]), .pin10(loader_addr[6]), .pin9(addr[6]));
  is61c64 chip_10__sram (
    .a12(ZERO), .a7(addr[7]), .a6(addr[6]), .a5(addr[5]), .a4(addr[4]), .a3(addr[3]), .a2(addr[2]),
    .a1(addr[1]), .a0(addr[0]), .io0(cw__2[16]), .io1(cw__2[17]), .io2(cw__2[18]), .io3(cw__2[19]),
    .io4(cw__2[20]), .io5(cw__2[21]), .io6(cw__2[22]), .io7(cw__2[23]), .ce_n(ZERO), .a10(addr[10]),
    .oe_n(oe_n), .a11(addr[11]), .a9(addr[9]), .a8(addr[8]), .we_n(we_pad[10]));
  is61c64 chip_2__sram (
    .a12(ZERO), .a7(addr[7]), .a6(addr[6]), .a5(addr[5]), .a4(addr[4]), .a3(addr[3]), .a2(addr[2]),
    .a1(addr[1]), .a0(addr[0]), .io0(cw__0[16]), .io1(cw__0[17]), .io2(cw__0[18]), .io3(cw__0[19]),
    .io4(cw__0[20]), .io5(cw__0[21]), .io6(cw__0[22]), .io7(cw__0[23]), .ce_n(ZERO), .a10(addr[10]),
    .oe_n(oe_n), .a11(addr[11]), .a9(addr[9]), .a8(addr[8]), .we_n(we_pad[2]));
  is61c64 chip_4__sram (
    .a12(ZERO), .a7(addr[7]), .a6(addr[6]), .a5(addr[5]), .a4(addr[4]), .a3(addr[3]), .a2(addr[2]),
    .a1(addr[1]), .a0(addr[0]), .io0(cw__1[0]), .io1(cw__1[1]), .io2(cw__1[2]), .io3(cw__1[3]),
    .io4(cw__1[4]), .io5(cw__1[5]), .io6(cw__1[6]), .io7(cw__1[7]), .ce_n(ZERO), .a10(addr[10]), .oe_n(oe_n),
    .a11(addr[11]), .a9(addr[9]), .a8(addr[8]), .we_n(we_pad[4]));
  is61c64 chip_6__sram (
    .a12(ZERO), .a7(addr[7]), .a6(addr[6]), .a5(addr[5]), .a4(addr[4]), .a3(addr[3]), .a2(addr[2]),
    .a1(addr[1]), .a0(addr[0]), .io0(cw__1[16]), .io1(cw__1[17]), .io2(cw__1[18]), .io3(cw__1[19]),
    .io4(cw__1[20]), .io5(cw__1[21]), .io6(cw__1[22]), .io7(cw__1[23]), .ce_n(ZERO), .a10(addr[10]),
    .oe_n(oe_n), .a11(addr[11]), .a9(addr[9]), .a8(addr[8]), .we_n(we_pad[6]));
  is61c64 chip_8__sram (
    .a12(ZERO), .a7(addr[7]), .a6(addr[6]), .a5(addr[5]), .a4(addr[4]), .a3(addr[3]), .a2(addr[2]),
    .a1(addr[1]), .a0(addr[0]), .io0(cw__2[0]), .io1(cw__2[1]), .io2(cw__2[2]), .io3(cw__2[3]),
    .io4(cw__2[4]), .io5(cw__2[5]), .io6(cw__2[6]), .io7(cw__2[7]), .ce_n(ZERO), .a10(addr[10]), .oe_n(oe_n),
    .a11(addr[11]), .a9(addr[9]), .a8(addr[8]), .we_n(we_pad[8]));
  _7432 ws0 (
    .pin1(cs_n[0]), .pin2(clk), .pin3(we_pad[0]), .pin4(cs_n[1]), .pin5(clk), .pin6(we_pad[1]), .pin13(clk),
    .pin12(cs_n[3]), .pin11(we_pad[3]), .pin10(clk), .pin9(cs_n[2]), .pin8(we_pad[2]));
  _74157 a2 (
    .pin1(loading), .pin2(upc[8]), .pin3(loader_addr[8]), .pin4(addr[8]), .pin5(upc[9]),
    .pin6(loader_addr[9]), .pin7(addr[9]), .pin15(ZERO), .pin14(upc[11]), .pin13(loader_addr[11]),
    .pin12(addr[11]), .pin11(upc[10]), .pin10(loader_addr[10]), .pin9(addr[10]));
  _74541 chip_10__wbuf (
    .pin1(wbuf_oe_n), .pin2(wdata[0]), .pin3(wdata[1]), .pin4(wdata[2]), .pin5(wdata[3]), .pin6(wdata[4]),
    .pin7(wdata[5]), .pin8(wdata[6]), .pin9(wdata[7]), .pin19(ZERO), .pin18(cw__2[16]), .pin17(cw__2[17]),
    .pin16(cw__2[18]), .pin15(cw__2[19]), .pin14(cw__2[20]), .pin13(cw__2[21]), .pin12(cw__2[22]),
    .pin11(cw__2[23]));
  _74541 chip_2__wbuf (
    .pin1(wbuf_oe_n), .pin2(wdata[0]), .pin3(wdata[1]), .pin4(wdata[2]), .pin5(wdata[3]), .pin6(wdata[4]),
    .pin7(wdata[5]), .pin8(wdata[6]), .pin9(wdata[7]), .pin19(ZERO), .pin18(cw__0[16]), .pin17(cw__0[17]),
    .pin16(cw__0[18]), .pin15(cw__0[19]), .pin14(cw__0[20]), .pin13(cw__0[21]), .pin12(cw__0[22]),
    .pin11(cw__0[23]));
  _74541 chip_4__wbuf (
    .pin1(wbuf_oe_n), .pin2(wdata[0]), .pin3(wdata[1]), .pin4(wdata[2]), .pin5(wdata[3]), .pin6(wdata[4]),
    .pin7(wdata[5]), .pin8(wdata[6]), .pin9(wdata[7]), .pin19(ZERO), .pin18(cw__1[0]), .pin17(cw__1[1]),
    .pin16(cw__1[2]), .pin15(cw__1[3]), .pin14(cw__1[4]), .pin13(cw__1[5]), .pin12(cw__1[6]), .pin11(cw__1[7]));
  _74541 chip_6__wbuf (
    .pin1(wbuf_oe_n), .pin2(wdata[0]), .pin3(wdata[1]), .pin4(wdata[2]), .pin5(wdata[3]), .pin6(wdata[4]),
    .pin7(wdata[5]), .pin8(wdata[6]), .pin9(wdata[7]), .pin19(ZERO), .pin18(cw__1[16]), .pin17(cw__1[17]),
    .pin16(cw__1[18]), .pin15(cw__1[19]), .pin14(cw__1[20]), .pin13(cw__1[21]), .pin12(cw__1[22]),
    .pin11(cw__1[23]));
  _74541 chip_8__wbuf (
    .pin1(wbuf_oe_n), .pin2(wdata[0]), .pin3(wdata[1]), .pin4(wdata[2]), .pin5(wdata[3]), .pin6(wdata[4]),
    .pin7(wdata[5]), .pin8(wdata[6]), .pin9(wdata[7]), .pin19(ZERO), .pin18(cw__2[0]), .pin17(cw__2[1]),
    .pin16(cw__2[2]), .pin15(cw__2[3]), .pin14(cw__2[4]), .pin13(cw__2[5]), .pin12(cw__2[6]), .pin11(cw__2[7]));
  _7432 ws1 (
    .pin1(cs_n[4]), .pin2(clk), .pin3(we_pad[4]), .pin4(cs_n[5]), .pin5(clk), .pin6(we_pad[5]), .pin13(clk),
    .pin12(cs_n[7]), .pin11(we_pad[7]), .pin10(clk), .pin9(cs_n[6]), .pin8(we_pad[6]));
  is61c64 chip_0__sram (
    .a12(ZERO), .a7(addr[7]), .a6(addr[6]), .a5(addr[5]), .a4(addr[4]), .a3(addr[3]), .a2(addr[2]),
    .a1(addr[1]), .a0(addr[0]), .io0(cw__0[0]), .io1(cw__0[1]), .io2(cw__0[2]), .io3(cw__0[3]),
    .io4(cw__0[4]), .io5(cw__0[5]), .io6(cw__0[6]), .io7(cw__0[7]), .ce_n(ZERO), .a10(addr[10]), .oe_n(oe_n),
    .a11(addr[11]), .a9(addr[9]), .a8(addr[8]), .we_n(we_pad[0]));
  is61c64 chip_1__sram (
    .a12(ZERO), .a7(addr[7]), .a6(addr[6]), .a5(addr[5]), .a4(addr[4]), .a3(addr[3]), .a2(addr[2]),
    .a1(addr[1]), .a0(addr[0]), .io0(cw__0[8]), .io1(cw__0[9]), .io2(cw__0[10]), .io3(cw__0[11]),
    .io4(cw__0[12]), .io5(cw__0[13]), .io6(cw__0[14]), .io7(cw__0[15]), .ce_n(ZERO), .a10(addr[10]),
    .oe_n(oe_n), .a11(addr[11]), .a9(addr[9]), .a8(addr[8]), .we_n(we_pad[1]));
  is61c64 chip_3__sram (
    .a12(ZERO), .a7(addr[7]), .a6(addr[6]), .a5(addr[5]), .a4(addr[4]), .a3(addr[3]), .a2(addr[2]),
    .a1(addr[1]), .a0(addr[0]), .io0(cw__0[24]), .io1(cw__0[25]), .io2(cw__0[26]), .io3(cw__0[27]),
    .io4(cw__0[28]), .io5(cw__0[29]), .io6(cw__0[30]), .io7(cw__0[31]), .ce_n(ZERO), .a10(addr[10]),
    .oe_n(oe_n), .a11(addr[11]), .a9(addr[9]), .a8(addr[8]), .we_n(we_pad[3]));
  is61c64 chip_5__sram (
    .a12(ZERO), .a7(addr[7]), .a6(addr[6]), .a5(addr[5]), .a4(addr[4]), .a3(addr[3]), .a2(addr[2]),
    .a1(addr[1]), .a0(addr[0]), .io0(cw__1[8]), .io1(cw__1[9]), .io2(cw__1[10]), .io3(cw__1[11]),
    .io4(cw__1[12]), .io5(cw__1[13]), .io6(cw__1[14]), .io7(cw__1[15]), .ce_n(ZERO), .a10(addr[10]),
    .oe_n(oe_n), .a11(addr[11]), .a9(addr[9]), .a8(addr[8]), .we_n(we_pad[5]));
  is61c64 chip_7__sram (
    .a12(ZERO), .a7(addr[7]), .a6(addr[6]), .a5(addr[5]), .a4(addr[4]), .a3(addr[3]), .a2(addr[2]),
    .a1(addr[1]), .a0(addr[0]), .io0(cw__1[24]), .io1(cw__1[25]), .io2(cw__1[26]), .io3(cw__1[27]),
    .io4(cw__1[28]), .io5(cw__1[29]), .io6(cw__1[30]), .io7(cw__1[31]), .ce_n(ZERO), .a10(addr[10]),
    .oe_n(oe_n), .a11(addr[11]), .a9(addr[9]), .a8(addr[8]), .we_n(we_pad[7]));
  is61c64 chip_9__sram (
    .a12(ZERO), .a7(addr[7]), .a6(addr[6]), .a5(addr[5]), .a4(addr[4]), .a3(addr[3]), .a2(addr[2]),
    .a1(addr[1]), .a0(addr[0]), .io0(cw__2[8]), .io1(cw__2[9]), .io2(cw__2[10]), .io3(cw__2[11]),
    .io4(cw__2[12]), .io5(cw__2[13]), .io6(cw__2[14]), .io7(cw__2[15]), .ce_n(ZERO), .a10(addr[10]),
    .oe_n(oe_n), .a11(addr[11]), .a9(addr[9]), .a8(addr[8]), .we_n(we_pad[9]));
  _7432 ws2 (
    .pin1(cs_n[8]), .pin2(clk), .pin3(we_pad[8]), .pin4(cs_n[9]), .pin5(clk), .pin6(we_pad[9]), .pin13(clk),
    .pin12(ZERO), .pin11(we_pad[11]), .pin10(clk), .pin9(cs_n[10]), .pin8(we_pad[10]));
  // also tied to GND on the sheet: ZERO
endmodule
