// Logisim project microsequencer.circ as structural Verilog: 1 circuit, main circuit microsequencer
module microsequencer (
  input  clk,
  input  clr_n,
  input  useq_op_0,
  input  useq_op_1,
  input  useq_op_2,
  input  next_addr_0,
  input  next_addr_1,
  input  next_addr_2,
  input  next_addr_3,
  input  next_addr_4,
  input  next_addr_5,
  input  next_addr_6,
  input  next_addr_7,
  input  next_addr_8,
  input  next_addr_9,
  input  next_addr_10,
  input  next_addr_11,
  input  ucond_sel_0,
  input  ucond_sel_1,
  input  ucond_sel_2,
  input  ucond_sel_3,
  input  ucond_pol,
  input  cond_0,
  input  cond_1,
  input  cond_2,
  input  cond_3,
  input  cond_4,
  input  cond_5,
  input  cond_6,
  input  cond_7,
  input  cond_8,
  input  cond_9,
  input  cond_10,
  input  cond_11,
  input  cond_12,
  input  cond_13,
  input  cond_14,
  input  cond_15,
  input  lut_data_0,
  input  lut_data_1,
  input  lut_data_2,
  input  lut_data_3,
  input  lut_data_4,
  input  lut_data_5,
  input  lut_data_6,
  input  lut_data_7,
  input  lut_data_8,
  input  lut_data_9,
  input  lut_data_10,
  input  lut_data_11,
  output upc_0,
  output upc_1,
  output upc_2,
  output upc_3,
  output upc_4,
  output upc_5,
  output upc_6,
  output upc_7,
  output upc_8,
  output upc_9,
  output upc_10,
  output upc_11
);

  wire and_y_0, and_y_1, and_y_2, and_y_3, branch_active, cond_hi, cond_lo, cond_raw, cond_taken, count_en,
       dispatch_active, do_load, inv_a_0, inv_a_1, inv_a_2, inv_a_3, inv_y_1, inv_y_3, inv_y_4, inv_y_5,
       merge_y_1, merge_y_2, merge_y_3, ONE, op_n_0, op_n_6, op_n_7, or_y_0, or_y_1, or_y_3, p_0, p_1, p_2,
       p_3, p_4, p_5, p_6, p_7, p_8, p_9, p_10, p_11, upc_rco_0, upc_rco_1, upc_rco_2, xor_y_1, xor_y_2,
       xor_y_3, ZERO;

  _7408 brand (
    .pin1(branch_active), .pin2(cond_taken), .pin3(and_y_0), .pin4(ZERO), .pin5(ZERO), .pin6(and_y_1),
    .pin13(ZERO), .pin12(ZERO), .pin11(and_y_3), .pin10(ZERO), .pin9(ZERO), .pin8(and_y_2));
  _7486 cpol (
    .pin1(cond_raw), .pin2(ucond_pol), .pin3(cond_taken), .pin4(ZERO), .pin5(ZERO), .pin6(xor_y_1),
    .pin13(ZERO), .pin12(ZERO), .pin11(xor_y_3), .pin10(ZERO), .pin9(ZERO), .pin8(xor_y_2));
  _74153 nmux_1__m (
    .pin1(ZERO), .pin2(inv_y_3), .pin3(ZERO), .pin4(ZERO), .pin5(lut_data_2), .pin6(next_addr_2), .pin7(p_2),
    .pin15(dispatch_active), .pin14(ZERO), .pin13(ZERO), .pin12(ZERO), .pin11(lut_data_3),
    .pin10(next_addr_3), .pin9(p_3));
  _74153 nmux_5__m (
    .pin1(ZERO), .pin2(inv_y_3), .pin3(ZERO), .pin4(ZERO), .pin5(lut_data_10), .pin6(next_addr_10),
    .pin7(p_10), .pin15(dispatch_active), .pin14(ZERO), .pin13(ZERO), .pin12(ZERO), .pin11(lut_data_11),
    .pin10(next_addr_11), .pin9(p_11));
  _74138 useq (
    .pin1(useq_op_0), .pin2(useq_op_1), .pin3(useq_op_2), .pin4(ZERO), .pin5(ZERO), .pin6(ONE),
    .pin7(op_n_7), .pin15(op_n_0), .pin14(inv_a_0), .pin13(inv_a_1), .pin12(inv_a_2), .pin11(inv_a_3),
    .pin10(count_en), .pin9(op_n_6));
  _74157 cmerge (
    .pin1(ucond_sel_3), .pin2(cond_lo), .pin3(cond_hi), .pin4(cond_raw), .pin5(ZERO), .pin6(ZERO),
    .pin7(merge_y_1), .pin15(ZERO), .pin14(ZERO), .pin13(ZERO), .pin12(merge_y_3), .pin11(ZERO),
    .pin10(ZERO), .pin9(merge_y_2));
  _7404 inv (
    .pin1(inv_a_0), .pin2(branch_active), .pin3(inv_a_1), .pin4(inv_y_1), .pin5(inv_a_2),
    .pin6(dispatch_active), .pin13(ZERO), .pin12(inv_y_5), .pin11(do_load), .pin10(inv_y_4), .pin9(inv_a_3),
    .pin8(inv_y_3));
  _74153 nmux_2__m (
    .pin1(ZERO), .pin2(inv_y_3), .pin3(ZERO), .pin4(ZERO), .pin5(lut_data_4), .pin6(next_addr_4), .pin7(p_4),
    .pin15(dispatch_active), .pin14(ZERO), .pin13(ZERO), .pin12(ZERO), .pin11(lut_data_5),
    .pin10(next_addr_5), .pin9(p_5));
  _74161 u0 (
    .pin1(clr_n), .pin2(clk), .pin3(p_0), .pin4(p_1), .pin5(p_2), .pin6(p_3), .pin7(count_en),
    .pin15(upc_rco_0), .pin14(upc_0), .pin13(upc_1), .pin12(upc_2), .pin11(upc_3), .pin10(count_en),
    .pin9(inv_y_4));
  _74151 cmux_hi (
    .pin1(cond_11), .pin2(cond_10), .pin3(cond_9), .pin4(cond_8), .pin5(cond_hi), .pin7(ZERO),
    .pin15(cond_12), .pin14(cond_13), .pin13(cond_14), .pin12(cond_15), .pin11(ucond_sel_0),
    .pin10(ucond_sel_1), .pin9(ucond_sel_2));  // open: pin6
  _7432 lor (
    .pin1(inv_y_1), .pin2(and_y_0), .pin3(or_y_0), .pin4(dispatch_active), .pin5(inv_y_3), .pin6(or_y_1),
    .pin13(ZERO), .pin12(ZERO), .pin11(or_y_3), .pin10(or_y_1), .pin9(or_y_0), .pin8(do_load));
  _74153 nmux_3__m (
    .pin1(ZERO), .pin2(inv_y_3), .pin3(ZERO), .pin4(ZERO), .pin5(lut_data_6), .pin6(next_addr_6), .pin7(p_6),
    .pin15(dispatch_active), .pin14(ZERO), .pin13(ZERO), .pin12(ZERO), .pin11(lut_data_7),
    .pin10(next_addr_7), .pin9(p_7));
  _74161 u1 (
    .pin1(clr_n), .pin2(clk), .pin3(p_4), .pin4(p_5), .pin5(p_6), .pin6(p_7), .pin7(count_en),
    .pin15(upc_rco_1), .pin14(upc_4), .pin13(upc_5), .pin12(upc_6), .pin11(upc_7), .pin10(upc_rco_0),
    .pin9(inv_y_4));
  _74151 cmux_lo (
    .pin1(cond_3), .pin2(cond_2), .pin3(cond_1), .pin4(cond_0), .pin5(cond_lo), .pin7(ZERO), .pin15(cond_4),
    .pin14(cond_5), .pin13(cond_6), .pin12(ONE), .pin11(ucond_sel_0), .pin10(ucond_sel_1), .pin9(ucond_sel_2));  // open: pin6
  _74153 nmux_0__m (
    .pin1(ZERO), .pin2(inv_y_3), .pin3(ZERO), .pin4(ZERO), .pin5(lut_data_0), .pin6(next_addr_0), .pin7(p_0),
    .pin15(dispatch_active), .pin14(ZERO), .pin13(ZERO), .pin12(ZERO), .pin11(lut_data_1),
    .pin10(next_addr_1), .pin9(p_1));
  _74153 nmux_4__m (
    .pin1(ZERO), .pin2(inv_y_3), .pin3(ZERO), .pin4(ZERO), .pin5(lut_data_8), .pin6(next_addr_8), .pin7(p_8),
    .pin15(dispatch_active), .pin14(ZERO), .pin13(ZERO), .pin12(ZERO), .pin11(lut_data_9),
    .pin10(next_addr_9), .pin9(p_9));
  _74161 u2 (
    .pin1(clr_n), .pin2(clk), .pin3(p_8), .pin4(p_9), .pin5(p_10), .pin6(p_11), .pin7(count_en),
    .pin15(upc_rco_2), .pin14(upc_8), .pin13(upc_9), .pin12(upc_10), .pin11(upc_11), .pin10(upc_rco_1),
    .pin9(inv_y_4));
  // also tied to GND on the sheet: ZERO
  // also tied to VCC on the sheet: ONE
endmodule
