// Logisim project opcode_lut.circ as structural Verilog: 2 circuits, main circuit opcode_lut
module is61c64 (
  input  a12,
  input  a7,
  input  a6,
  input  a5,
  input  a4,
  input  a3,
  input  a2,
  input  a1,
  input  a0,
  input  ce_n,
  input  a10,
  input  oe_n,
  input  a11,
  input  a9,
  input  a8,
  input  we_n,
  output io0,
  output io1,
  output io2,
  output io3,
  output io4,
  output io5,
  output io6,
  output io7
);
endmodule

module opcode_lut (
  input  clk,
  input  [11:0] loader_addr,
  input  dispatch_page,
  input  [7:0] ir,
  input  loading,
  input  [7:0] wdata,
  input  wbuf_oe_n,
  input  oe_n,
  input  [1:0] cs_n,
  output [7:0] lut_lo,
  output [7:0] lut_hi
);

  wire ZERO;
  wire [3:0] we_pad;
  wire [11:0] addr;

  _74157 a0 (
    .pin1(loading), .pin2(ir[0]), .pin3(loader_addr[0]), .pin4(addr[0]), .pin5(ir[1]), .pin6(loader_addr[1]),
    .pin7(addr[1]), .pin15(ZERO), .pin14(ir[3]), .pin13(loader_addr[3]), .pin12(addr[3]), .pin11(ir[2]),
    .pin10(loader_addr[2]), .pin9(addr[2]));
  _74541 chip_0__wbuf (
    .pin1(wbuf_oe_n), .pin2(wdata[0]), .pin3(wdata[1]), .pin4(wdata[2]), .pin5(wdata[3]), .pin6(wdata[4]),
    .pin7(wdata[5]), .pin8(wdata[6]), .pin9(wdata[7]), .pin19(ZERO), .pin18(lut_lo[0]), .pin17(lut_lo[1]),
    .pin16(lut_lo[2]), .pin15(lut_lo[3]), .pin14(lut_lo[4]), .pin13(lut_lo[5]), .pin12(lut_lo[6]),
    .pin11(lut_lo[7]));
  _74157 a1 (
    .pin1(loading), .pin2(ir[4]), .pin3(loader_addr[4]), .pin4(addr[4]), .pin5(ir[5]), .pin6(loader_addr[5]),
    .pin7(addr[5]), .pin15(ZERO), .pin14(ir[7]), .pin13(loader_addr[7]), .pin12(addr[7]), .pin11(ir[6]),
    .pin10(loader_addr[6]), .pin9(addr[6]));
  is61c64 chip_1__sram (
    .a12(ZERO), .a7(addr[7]), .a6(addr[6]), .a5(addr[5]), .a4(addr[4]), .a3(addr[3]), .a2(addr[2]),
    .a1(addr[1]), .a0(addr[0]), .io0(lut_hi[0]), .io1(lut_hi[1]), .io2(lut_hi[2]), .io3(lut_hi[3]),
    .io4(lut_hi[4]), .io5(lut_hi[5]), .io6(lut_hi[6]), .io7(lut_hi[7]), .ce_n(ZERO), .a10(addr[10]),
    .oe_n(oe_n), .a11(addr[11]), .a9(addr[9]), .a8(addr[8]), .we_n(we_pad[1]));
  _74157 a2 (
    .pin1(loading), .pin2(dispatch_page), .pin3(loader_addr[8]), .pin4(addr[8]), .pin5(ZERO),
    .pin6(loader_addr[9]), .pin7(addr[9]), .pin15(ZERO), .pin14(ZERO), .pin13(loader_addr[11]),
    .pin12(addr[11]), .pin11(ZERO), .pin10(loader_addr[10]), .pin9(addr[10]));
  _74541 chip_1__wbuf (
    .pin1(wbuf_oe_n), .pin2(wdata[0]), .pin3(wdata[1]), .pin4(wdata[2]), .pin5(wdata[3]), .pin6(wdata[4]),
    .pin7(wdata[5]), .pin8(wdata[6]), .pin9(wdata[7]), .pin19(ZERO), .pin18(lut_hi[0]), .pin17(lut_hi[1]),
    .pin16(lut_hi[2]), .pin15(lut_hi[3]), .pin14(lut_hi[4]), .pin13(lut_hi[5]), .pin12(lut_hi[6]),
    .pin11(lut_hi[7]));
  is61c64 chip_0__sram (
    .a12(ZERO), .a7(addr[7]), .a6(addr[6]), .a5(addr[5]), .a4(addr[4]), .a3(addr[3]), .a2(addr[2]),
    .a1(addr[1]), .a0(addr[0]), .io0(lut_lo[0]), .io1(lut_lo[1]), .io2(lut_lo[2]), .io3(lut_lo[3]),
    .io4(lut_lo[4]), .io5(lut_lo[5]), .io6(lut_lo[6]), .io7(lut_lo[7]), .ce_n(ZERO), .a10(addr[10]),
    .oe_n(oe_n), .a11(addr[11]), .a9(addr[9]), .a8(addr[8]), .we_n(we_pad[0]));
  _7432 ws (
    .pin1(cs_n[0]), .pin2(clk), .pin3(we_pad[0]), .pin4(cs_n[1]), .pin5(clk), .pin6(we_pad[1]), .pin13(clk),
    .pin12(ZERO), .pin11(we_pad[3]), .pin10(clk), .pin9(ZERO), .pin8(we_pad[2]));
  // also tied to GND on the sheet: ZERO

  // Other names for the same wires on the sheet: _0_io_0__7_0_[7:0] = lut_lo; _0_io_1__7_0_[7:0] = lut_hi;
  //   run_addr[8:0] = {dispatch_page, ir}
endmodule
