// Logisim project uc_loader.circ as structural Verilog: 2 circuits, main circuit uc_loader
module sst39sf010a (
  input  a16,
  input  a15,
  input  a12,
  input  a7,
  input  a6,
  input  a5,
  input  a4,
  input  a3,
  input  a2,
  input  a1,
  input  a0,
  input  ce_n,
  input  a10,
  input  oe_n,
  input  a11,
  input  a9,
  input  a8,
  input  a13,
  input  a14,
  input  we_n,
  output dq0,
  output dq1,
  output dq2,
  output dq3,
  output dq4,
  output dq5,
  output dq6,
  output dq7
);
endmodule

module uc_loader (
  input  clk,
  input  rst_n,
  output [11:0] sram_addr,
  output [7:0] sram_wdata,
  output [12:0] cs_n,
  output loading
);

  wire ONE, ZERO;
  wire [3:0] rco;
  wire [7:6] dhi;
  wire [15:12] cnt;

  _74161 c0 (
    .pin1(rst_n), .pin2(clk), .pin3(ZERO), .pin4(ZERO), .pin5(ZERO), .pin6(ZERO), .pin7(loading),
    .pin15(rco[0]), .pin14(sram_addr[0]), .pin13(sram_addr[1]), .pin12(sram_addr[2]), .pin11(sram_addr[3]),
    .pin10(loading), .pin9(ONE));
  _74138 dec_hi (
    .pin1(cnt[12]), .pin2(cnt[13]), .pin3(cnt[14]), .pin4(ZERO), .pin5(ZERO), .pin6(cnt[15]), .pin7(dhi[7]),
    .pin15(cs_n[8]), .pin14(cs_n[9]), .pin13(cs_n[10]), .pin12(cs_n[11]), .pin11(cs_n[12]), .pin10(loading),
    .pin9(dhi[6]));
  _74161 c1 (
    .pin1(rst_n), .pin2(clk), .pin3(ZERO), .pin4(ZERO), .pin5(ZERO), .pin6(ZERO), .pin7(loading),
    .pin15(rco[1]), .pin14(sram_addr[4]), .pin13(sram_addr[5]), .pin12(sram_addr[6]), .pin11(sram_addr[7]),
    .pin10(rco[0]), .pin9(ONE));
  _74138 dec_lo (
    .pin1(cnt[12]), .pin2(cnt[13]), .pin3(cnt[14]), .pin4(cnt[15]), .pin5(ZERO), .pin6(ONE), .pin7(cs_n[7]),
    .pin15(cs_n[0]), .pin14(cs_n[1]), .pin13(cs_n[2]), .pin12(cs_n[3]), .pin11(cs_n[4]), .pin10(cs_n[5]),
    .pin9(cs_n[6]));
  _74161 c2 (
    .pin1(rst_n), .pin2(clk), .pin3(ZERO), .pin4(ZERO), .pin5(ZERO), .pin6(ZERO), .pin7(loading),
    .pin15(rco[2]), .pin14(sram_addr[8]), .pin13(sram_addr[9]), .pin12(sram_addr[10]), .pin11(sram_addr[11]),
    .pin10(rco[1]), .pin9(ONE));
  sst39sf010a eeprom (
    .a16(ZERO), .a15(cnt[15]), .a12(cnt[12]), .a7(sram_addr[7]), .a6(sram_addr[6]), .a5(sram_addr[5]),
    .a4(sram_addr[4]), .a3(sram_addr[3]), .a2(sram_addr[2]), .a1(sram_addr[1]), .a0(sram_addr[0]),
    .dq0(sram_wdata[0]), .dq1(sram_wdata[1]), .dq2(sram_wdata[2]), .dq3(sram_wdata[3]), .dq4(sram_wdata[4]),
    .dq5(sram_wdata[5]), .dq6(sram_wdata[6]), .dq7(sram_wdata[7]), .ce_n(ZERO), .a10(sram_addr[10]),
    .oe_n(ZERO), .a11(sram_addr[11]), .a9(sram_addr[9]), .a8(sram_addr[8]), .a13(cnt[13]), .a14(cnt[14]),
    .we_n(ONE));
  _74161 c3 (
    .pin1(rst_n), .pin2(clk), .pin3(ZERO), .pin4(ZERO), .pin5(ZERO), .pin6(ZERO), .pin7(loading),
    .pin15(rco[3]), .pin14(cnt[12]), .pin13(cnt[13]), .pin12(cnt[14]), .pin11(cnt[15]), .pin10(rco[2]),
    .pin9(ONE));
  // also tied to GND on the sheet: ZERO
  // also tied to VCC on the sheet: ONE

  // Other names for the same wires on the sheet: cnt[11:0] = sram_addr; dhi[5] = loading; rom_data[7:0] = sram_wdata
endmodule
